// Logisim project ALU2021-KL0902.circ as structural Verilog: 5 circuits, main circuit 1-1  8位加法器
module \_1_1__8位加法器  (
  input  [7:0] X,
  input  [7:0] Y,
  input  Cin,
  output [7:0] S,
  output Cout,
  output OF
);

  wire \n1位全加器_2_cout , \n1位全加器_3_cout , \n1位全加器_4_cout , \n1位全加器_5_cout , \n1位全加器_6_cout , \n1位全加器_7_cout ,
       \n1位全加器_8_cout ;

  xor xor_1 (OF, \n1位全加器_2_cout , Cout);
  \_1位全加器  \u_1位全加器_1  (.Cout(Cout), .Si(S[7]), .Cin(\n1位全加器_2_cout ), .Xi(X[7]), .Yi(Y[7]));
  \_1位全加器  \u_1位全加器_2  (.Cout(\n1位全加器_2_cout ), .Si(S[6]), .Cin(\n1位全加器_3_cout ), .Xi(X[6]), .Yi(Y[6]));
  \_1位全加器  \u_1位全加器_3  (.Cout(\n1位全加器_3_cout ), .Si(S[5]), .Cin(\n1位全加器_4_cout ), .Xi(X[5]), .Yi(Y[5]));
  \_1位全加器  \u_1位全加器_4  (.Cout(\n1位全加器_4_cout ), .Si(S[4]), .Cin(\n1位全加器_5_cout ), .Xi(X[4]), .Yi(Y[4]));
  \_1位全加器  \u_1位全加器_5  (.Cout(\n1位全加器_5_cout ), .Si(S[3]), .Cin(\n1位全加器_6_cout ), .Xi(X[3]), .Yi(Y[3]));
  \_1位全加器  \u_1位全加器_6  (.Cout(\n1位全加器_6_cout ), .Si(S[2]), .Cin(\n1位全加器_7_cout ), .Xi(X[2]), .Yi(Y[2]));
  // Probe on X
  // Probe on Y
  // Probe on S
  \_1位全加器  \u_1位全加器_7  (.Cout(\n1位全加器_7_cout ), .Si(S[1]), .Cin(\n1位全加器_8_cout ), .Xi(X[1]), .Yi(Y[1]));
  \_1位全加器  \u_1位全加器_8  (.Cout(\n1位全加器_8_cout ), .Si(S[0]), .Cin(Cin), .Xi(X[0]), .Yi(Y[0]));
  // Probe on X
  // Probe on Y
  // Probe on S

  // Notes on the sheet:
  //   输入引脚区
  //   注：不能增加任何输入输出端口信号
  //   （1）使用1位全加器FA实现8位加法器，给出溢出标志OF
  //   输出引脚区
  //   =
  //   有符号数
  //   （2）封装电路供后续实验使用
  //   =
  //   结果测试区
  //   无符号数
endmodule

module \_1_2_32位可控加减器  (
  input  Sub,
  input  [31:0] X,
  input  [31:0] Y,
  output CF,
  output OF,
  output ZF,
  output SF,
  output [31:0] S
);

  wire and_1_out, comparator_1_eq, \n1_1_8位加法器_2_cout , \n1_1_8位加法器_3_cout , \n1_1_8位加法器_4_cout ;
  wire [2:0] multiplexer_2_out, multiplexer_2_out_2, multiplexer_2_out_3;
  wire [7:0] multiplexer_1_out, multiplexer_1_out_2, multiplexer_1_out_3, multiplexer_1_out_4;
  wire [31:0] bit_extender_1_out, xor_1_out;

  \_1_1__8位加法器  \u_1_1_8位加法器_1  (
    .X(X[31:24]), .Y(multiplexer_1_out_4), .Cin(\n1_1_8位加法器_2_cout ), .S(S[31:24]), .Cout(CF), .OF(OF));
  \_1_1__8位加法器  \u_1_1_8位加法器_2  (
    .X(X[23:16]), .Y(multiplexer_1_out_3), .Cin(\n1_1_8位加法器_3_cout ), .S(S[23:16]), .Cout(\n1_1_8位加法器_2_cout ));  // open: OF
  // Probe on X
  // Probe on Y
  // Probe on S
  \_1_1__8位加法器  \u_1_1_8位加法器_3  (
    .X(X[15:8]), .Y(multiplexer_1_out_2), .Cin(\n1_1_8位加法器_4_cout ), .S(S[15:8]), .Cout(\n1_1_8位加法器_3_cout ));  // open: OF
  Comparator #(.width(32), .mode("twosComplement")) comparator_1 (
    .a({32{1'b0}}), .b(Y), .eq(comparator_1_eq));  // open: gt, lt
  Multiplexer #(.select(1), .width(32), .disabled("Z"), .enable("false")) multiplexer_1 (
    .in0(xor_1_out), .in1({32{1'b0}}),
    .out({multiplexer_1_out_4, multiplexer_1_out_3, multiplexer_1_out_2, multiplexer_1_out}),
    .sel(comparator_1_eq));
  // Probe on X
  // Probe on Y
  // Probe on S
  \_1_1__8位加法器  \u_1_1_8位加法器_4  (
    .X(X[7:0]), .Y(multiplexer_1_out), .Cin(and_1_out), .S(S[7:0]), .Cout(\n1_1_8位加法器_4_cout ));  // open: OF
  assign xor_1_out = bit_extender_1_out ^ Y;  // XOR_Gate xor_1, 32 bits wide
  and and_1 (and_1_out, Sub, ~comparator_1_eq);  // AND_Gate
  nor nor_1 (ZF, S[0], S[1], S[2], S[3], S[4], S[5], S[6], S[7], S[8], S[9], S[10], S[11], S[12], S[13], S[14], S[15], S[17], S[18], S[19], S[20], S[21], S[22], S[23], S[24], S[25], S[26], S[27], S[28], S[29], S[30], S[31], S[16]);
  assign bit_extender_1_out = {{31{Sub}}, Sub};  // Bit_Extender bit_extender_1
  DotMatrix #(.inputtype("column"), .matrixcols(3), .matrixrows(3), .persist(0), .dotshape("square")) dotmatrix_1 (
    .col0(multiplexer_2_out_3), .col1(multiplexer_2_out_2), .col2(multiplexer_2_out));
  Multiplexer #(.select(1), .width(9), .disabled("Z"), .enable("false")) multiplexer_2 (
    .in0(9'hba), .in1(9'h92), .out({multiplexer_2_out_3, multiplexer_2_out_2, multiplexer_2_out}), .sel(Sub));

  assign SF = S[31];

  // Notes on the sheet:
  //   输入引脚区
  //   注：不能增加任何输入输出端口信号
  //   用封装后的8位加法器构成32位加减可控运算器，并产生正确的标志位
  //   输出引脚区
  //   =
  //   有符号数
  //   =
  //   结果测试区
  //   无符号数
endmodule

module \_1_3_32位ALU  (
  input  [2:0] AluOp,
  input  [31:0] X,
  input  [31:0] Y,
  output OF,
  output UOF,
  output ZF,
  output [31:0] S
);

  wire comparator_1_lt, decoder_1_out1, \n1_2_32位可控加减器_1_cf , \n1_2_32位可控加减器_1_of ;
  wire [31:0] and_1_out, bit_extender_1_out, \n1_2_32位可控加减器_1_s , not_1_out, or_1_out, xor_1_out;

  Decoder #(.select(3), .tristate("false"), .disabled("Z"), .enable("false")) decoder_1 (
    .out1(decoder_1_out1), .sel(AluOp));  // open: out0, out2, out3, out4, out5, out6, out7
  \_1_2_32位可控加减器  \u_1_2_32位可控加减器_1  (
    .X(X), .Y(Y), .Sub(decoder_1_out1), .S(\n1_2_32位可控加减器_1_s ), .CF(\n1_2_32位可控加减器_1_cf ),
    .OF(\n1_2_32位可控加减器_1_of ));  // open: ZF, SF
  assign or_1_out = X | Y;  // OR_Gate or_1, 32 bits wide
  assign and_1_out = X & Y;  // AND_Gate and_1, 32 bits wide
  assign xor_1_out = X ^ Y;  // XOR_Gate xor_1, 32 bits wide
  Comparator #(.width(32), .mode("twosComplement")) comparator_1 (.a(X), .b(Y), .lt(comparator_1_lt));  // open: gt, eq
  // Probe on X
  // Probe on Y
  // Probe on S
  assign bit_extender_1_out = {{31{1'b0}}, comparator_1_lt};  // Bit_Extender bit_extender_1
  assign not_1_out = ~Y;  // NOT_Gate not_1, 32 bits wide
  // Probe on X
  // Probe on Y
  // Probe on S
  Multiplexer #(.select(3), .width(32), .disabled("Z"), .enable("false")) multiplexer_1 (
    .in0(\n1_2_32位可控加减器_1_s ), .in1(\n1_2_32位可控加减器_1_s ), .in2(and_1_out), .in3(or_1_out), .in4(xor_1_out),
    .in5(Y), .in6(not_1_out), .in7(bit_extender_1_out), .out(S), .sel(AluOp));
  Multiplexer #(.select(3), .width(1), .disabled("Z"), .enable("false")) multiplexer_2 (
    .in0(\n1_2_32位可控加减器_1_of ), .in1(\n1_2_32位可控加减器_1_of ), .in2(1'b0), .in3(1'b0), .in4(1'b0), .in5(1'b0),
    .in6(1'b0), .in7(1'b0), .out(OF), .sel(AluOp));
  Multiplexer #(.select(3), .width(1), .disabled("Z"), .enable("false")) multiplexer_3 (
    .in0(\n1_2_32位可控加减器_1_cf ), .in1(comparator_1_lt), .in2(1'b0), .in3(1'b0), .in4(1'b0), .in5(1'b0),
    .in6(1'b0), .in7(1'b0), .out(UOF), .sel(AluOp));
  Comparator #(.width(32), .mode("unsigned")) comparator_2 (.a(S), .b({32{1'b0}}), .eq(ZF));  // open: gt, lt

  // Notes on the sheet:
  //   输入引脚区
  //   000 ：S=X+Y
  //   注：不能增加任何输入输出端口信号
  //   001：S=X-Y
  //   010 ：S=X&Y
  //   实现一个32位的ALU，可以由AluOP控制实现8种运算操作，并产生正确的标志位。AluOp与运算关系如下：
  //   011：S=X|Y
  //   输出引脚区
  //   100 ：S=X^Y
  //   =
  //   有符号数
  //   101 ：S=Y
  //   110 ：S=~Y
  //   =
  //   结果测试区
  //   无符号数
  //   111 ：S=X<Y?1:0
endmodule

module \_1_4_补码一位乘法器  (
  input  [7:0] X,
  input  [7:0] Y,
  output [15:0] S
);

  wire and_1_out, clock_1_out, comparator_1_eq, comparator_2_eq, not_2_out, Reset;
  wire [0:0] \n1_1_8位加法器_1_s_2 ;
  wire [1:1] Yn_1_q;
  wire [7:0] multiplexer_1_out, multiplexer_2_out, \n1_1_8位加法器_1_s , \n1_1_8位加法器_2_s , not_1_out,
       register_1_q;

  Clock #(.highDuration(1), .lowDuration(1)) clock_1 (.out(clock_1_out));
  Button \u_复位  (.out(Reset));
  // Probe on S[15:8]
  Register #(.width(8), .trigger("rising"), .Select("low")) \u_Σ_2  (
    .D({{2{\n1_1_8位加法器_1_s [7]}}, \n1_1_8位加法器_1_s [5:0]}), .en(not_2_out), .Q(S[15:8]), .clk(clock_1_out),
    .clr(Reset));
  \_1_1__8位加法器  \u_1_1_8位加法器_1  (
    .X(S[15:8]), .Y(multiplexer_1_out), .Cin(and_1_out),
    .S({\n1_1_8位加法器_1_s [7], \n1_1_8位加法器_1_s [5:0], \n1_1_8位加法器_1_s_2 [0]}));  // open: Cout, OF
  Multiplexer #(.select(2), .width(8), .disabled("Z"), .enable("false")) multiplexer_1 (
    .in0({8{1'b0}}), .in1(not_1_out), .in2(X), .in3({8{1'b0}}), .out(multiplexer_1_out),
    .sel({Yn_1_q[1], S[0]}));
  assign not_1_out = ~X;  // NOT_Gate not_1, 8 bits wide
  Register #(.width(8), .trigger("rising"), .Select("low")) u_Y (
    .D(multiplexer_2_out), .en(not_2_out), .Q(S[7:0]), .clk(clock_1_out), .clr(Reset));
  Multiplexer #(.select(1), .width(8), .disabled("Z"), .enable("false")) multiplexer_2 (
    .in0({\n1_1_8位加法器_1_s_2 [0], S[7:1]}), .in1(Y), .out(multiplexer_2_out), .sel(comparator_1_eq));
  // Probe on S[7:0]
  Register #(.width(1), .trigger("rising"), .Select("low")) Yn_1 (
    .D(S[0]), .en(not_2_out), .Q(Yn_1_q[1]), .clk(clock_1_out), .clr(Reset));
  // Probe on Yn_1_q[1]
  and and_1 (and_1_out, ~Yn_1_q[1], S[0]);  // AND_Gate
  Register #(.width(8), .trigger("rising"), .Select("low")) register_1 (
    .D(\n1_1_8位加法器_2_s ), .en(not_2_out), .Q(register_1_q), .clk(clock_1_out), .clr(Reset));
  // Probe on X
  // Probe on Y
  // Probe on S
  Comparator #(.width(8), .mode("unsigned")) comparator_1 (
    .a(register_1_q), .b({8{1'b0}}), .eq(comparator_1_eq));  // open: gt, lt
  Comparator #(.width(8), .mode("unsigned")) comparator_2 (
    .a(register_1_q), .b(8'h9), .eq(comparator_2_eq));  // open: gt, lt
  not not_2 (not_2_out, comparator_2_eq);
  \_1_1__8位加法器  \u_1_1_8位加法器_2  (.X(register_1_q), .Y(8'h1), .Cin(1'b0), .S(\n1_1_8位加法器_2_s ));  // open: Cout, OF

  // Other names for the same wires on the sheet: 乘积[15:0] = S

  // Notes on the sheet:
  //   注：不能增加任何输入输出端口信号
  //   输入引脚区
  //   算术右移1位
  //   功能说明：补码一位乘法器，S=X×Y，要求采用Booth乘法实现，最终结果输出到乘积引脚上。
  //   输出引脚区
  //   =
  //   有符号数
  //   核心算法：｛∑，Y｝=｛∑，( Yn+1-Yn ) [X]    ,    Y }  / 2
  //   结果测试区
  //   补
endmodule

module \_1位全加器  (
  input  Cin,
  input  Xi,
  input  Yi,
  output Cout,
  output Si
);

  wire and_1_out, and_2_out, xor_2_out;

  and and_1 (and_1_out, Xi, Yi);
  or or_1 (Cout, and_1_out, and_2_out);
  and and_2 (and_2_out, Cin, xor_2_out);
  xor xor_1 (Si, Cin, xor_2_out);
  xor xor_2 (xor_2_out, Xi, Yi);
endmodule
