// Logisim project LED.circ as structural Verilog: 1 circuit, main circuit NeverGonnaGiveYouUp
module NeverGonnaGiveYouUp (
  input  Clk,
  input  Reset,
  input  Pause,
  output [31:0] out_4,
  output [31:0] out_5,
  output [31:0] out_6,
  output [31:0] out_7,
  output [31:0] out_8,
  output [31:0] out_9,
  output [31:0] out_10,
  output [31:0] out_11,
  output [31:0] out_12,
  output [31:0] out_13,
  output [31:0] out_14,
  output [31:0] out_15,
  output [31:0] out_16,
  output [31:0] out_17,
  output [31:0] out_18,
  output [31:0] out_19,
  output [31:0] out_20,
  output [31:0] out_21,
  output [31:0] out_22,
  output [31:0] out_23,
  output [31:0] out_24,
  output [31:0] out_25,
  output [31:0] out_26,
  output [31:0] out_27,
  output [31:0] out_28,
  output [31:0] out_29,
  output [31:0] out_30,
  output [31:0] out_31,
  output [31:0] out_32,
  output [31:0] out_33,
  output [31:0] out_34,
  output [31:0] out_35
);

  wire or_1_out;
  wire [11:0] counter_1_q;

  Counter #(.width(12), .max('hc6d), .ongoal("wrap"), .trigger("rising"), .behavior("old")) counter_1 (
    .Q(counter_1_q), .clk(or_1_out), .clr(Reset));  // open: load, D, count, carry, preset
  or or_1 (or_1_out, Clk, Pause);
  ROM #(.addrWidth(12), .dataWidth(32), .Select("high")) rom_1 (.addr(counter_1_q), .data(out_4));
  ROM #(.addrWidth(12), .dataWidth(32), .Select("high")) rom_2 (.addr(counter_1_q), .data(out_5));
  ROM #(.addrWidth(12), .dataWidth(32), .Select("high")) rom_3 (.addr(counter_1_q), .data(out_6));
  ROM #(.addrWidth(12), .dataWidth(32), .Select("high")) rom_4 (.addr(counter_1_q), .data(out_7));
  ROM #(.addrWidth(12), .dataWidth(32), .Select("high")) rom_5 (.addr(counter_1_q), .data(out_8));
  ROM #(.addrWidth(12), .dataWidth(32), .Select("high")) rom_6 (.addr(counter_1_q), .data(out_9));
  ROM #(.addrWidth(12), .dataWidth(32), .Select("high")) rom_7 (.addr(counter_1_q), .data(out_10));
  ROM #(.addrWidth(12), .dataWidth(32), .Select("high")) rom_8 (.addr(counter_1_q), .data(out_11));
  ROM #(.addrWidth(12), .dataWidth(32), .Select("high")) rom_9 (.addr(counter_1_q), .data(out_12));
  ROM #(.addrWidth(12), .dataWidth(32), .Select("high")) rom_10 (.addr(counter_1_q), .data(out_13));
  ROM #(.addrWidth(12), .dataWidth(32), .Select("high")) rom_11 (.addr(counter_1_q), .data(out_14));
  ROM #(.addrWidth(12), .dataWidth(32), .Select("high")) rom_12 (.addr(counter_1_q), .data(out_15));
  ROM #(.addrWidth(12), .dataWidth(32), .Select("high")) rom_13 (.addr(counter_1_q), .data(out_16));
  ROM #(.addrWidth(12), .dataWidth(32), .Select("high")) rom_14 (.addr(counter_1_q), .data(out_17));
  ROM #(.addrWidth(12), .dataWidth(32), .Select("high")) rom_15 (.addr(counter_1_q), .data(out_18));
  ROM #(.addrWidth(12), .dataWidth(32), .Select("high")) rom_16 (.addr(counter_1_q), .data(out_19));
  ROM #(.addrWidth(12), .dataWidth(32), .Select("high")) rom_17 (.addr(counter_1_q), .data(out_20));
  ROM #(.addrWidth(12), .dataWidth(32), .Select("high")) rom_18 (.addr(counter_1_q), .data(out_21));
  ROM #(.addrWidth(12), .dataWidth(32), .Select("high")) rom_19 (.addr(counter_1_q), .data(out_22));
  ROM #(.addrWidth(12), .dataWidth(32), .Select("high")) rom_20 (.addr(counter_1_q), .data(out_23));
  ROM #(.addrWidth(12), .dataWidth(32), .Select("high")) rom_21 (.addr(counter_1_q), .data(out_24));
  ROM #(.addrWidth(12), .dataWidth(32), .Select("high")) rom_22 (.addr(counter_1_q), .data(out_25));
  ROM #(.addrWidth(12), .dataWidth(32), .Select("high")) rom_23 (.addr(counter_1_q), .data(out_26));
  ROM #(.addrWidth(12), .dataWidth(32), .Select("high")) rom_24 (.addr(counter_1_q), .data(out_27));
  ROM #(.addrWidth(12), .dataWidth(32), .Select("high")) rom_25 (.addr(counter_1_q), .data(out_28));
  ROM #(.addrWidth(12), .dataWidth(32), .Select("high")) rom_26 (.addr(counter_1_q), .data(out_29));
  ROM #(.addrWidth(12), .dataWidth(32), .Select("high")) rom_27 (.addr(counter_1_q), .data(out_30));
  ROM #(.addrWidth(12), .dataWidth(32), .Select("high")) rom_28 (.addr(counter_1_q), .data(out_31));
  ROM #(.addrWidth(12), .dataWidth(32), .Select("high")) rom_29 (.addr(counter_1_q), .data(out_32));
  ROM #(.addrWidth(12), .dataWidth(32), .Select("high")) rom_30 (.addr(counter_1_q), .data(out_33));
  ROM #(.addrWidth(12), .dataWidth(32), .Select("high")) rom_31 (.addr(counter_1_q), .data(out_34));
  ROM #(.addrWidth(12), .dataWidth(32), .Select("high")) rom_32 (.addr(counter_1_q), .data(out_35));
  DotMatrix #(.inputtype("column"), .matrixcols(32), .matrixrows(32), .persist(0), .dotshape("square")) dotmatrix_1 (
    .col0(out_4), .col1(out_5), .col2(out_6), .col3(out_7), .col4(out_8), .col5(out_9), .col6(out_10),
    .col7(out_11), .col8(out_12), .col9(out_13), .col10(out_14), .col11(out_15), .col12(out_16),
    .col13(out_17), .col14(out_18), .col15(out_19), .col16(out_20), .col17(out_21), .col18(out_22),
    .col19(out_23), .col20(out_24), .col21(out_25), .col22(out_26), .col23(out_27), .col24(out_28),
    .col25(out_29), .col26(out_30), .col27(out_31), .col28(out_32), .col29(out_33), .col30(out_34),
    .col31(out_35));

  // Notes on the sheet:
  //   contents of rom_1 (hex, n*v repeats v):
  //   0 fffffff8 fffffffc fffffffe 4*ffffffff fffffffe fffffffe 4*ffffffff 7c fff0007c 13*fffffffc
  //   ffffffff ffffffff fffffffe 78000000 0 7ff 1c00 ffffffff ffffffff ffffffff ffffffc2 ffffff80 ffffff00
  //   ffffff00 ffffff80 fffffffc 21*ffffffff fffffff8 fffffff8 fffffff8 fffffffc 28*ffffffff fffffeff
  //   ffffc07f ffffc07f ffffe03f fffff03f ffffff7f 7*ffffffff ff7 7fc ff 7f a80147f 107f c7f 67f 8*0 100
  //   700 100 0 1f18c 1f180 4*1f380 3f300 3f700 3f700 3ff00 fffffffe ffffffff ffffffff fffffffc fffffffe
  //   23*ffffffff f7fcf800 fffdf800 7ffffe00 7ffffe00 ffffff00 ffffffc2 ffffffc7 ffffffe4 ffffffff
  //   7fffffff ffffffff ffffff80 ffffffc0 ffffffc0 ffffffe0 ffffffe0 fffffff0 fffffff0 fffffff8 fffffffc
  //   fffffffc ffffffec 7fffffc0 7*0 60000000 6*fffffffe 16*ffffffff ffffffe0 fffffff0 fffffffc ffffefff
  //   16*ffffffff ffffe7ff ffffe7ff ffffcfff ffffe7ff fffff9ff ffffffff ffffffff ffff8fff 7*ffffffff
  //   fff9ffff ffffffff ffffffff ffffffff fffffffe 4*ffffffff fffe1fff ffffffff ffffffff fffff0ff ffffffff
  //   ffffffff ffffffff 9*0 3ec 2c 1fe 5ffe fffe fffe 17f4 17f0 8*0 7e ff 1ffff 1fffff 17f9fffe 3f97ffc 70
  //   f8 1f8 fe 7e 11 7*0 1b0 7ff 3fff 7ffc 3ffe 3ffe 7d88146 101fc6 6 1f 3f ff 4*3ff 7ff fff 3fff ffff
  //   1ffff ffff 7fff 3fff fff 1ff 7 ffffffee fffffffe fffffffc fffffffe fffffffe 0 ffe00000 17*ffffffff
  //   7fffffff 7fffffff fffffffe fffffffe 31fffffa 20604081 ffffffff ffffffff fffffeff ffffffff 8fffffff
  //   7fffff 3ffff 2ffff 1ffff 8005ffff 800dffff 400fffff c006ffff e0037fff c001ffff 8000f8ff 1ffff 77fff
  //   2fffff efffff fffffff 1ffdf7ff 8fffbfff cfffbfff fffe9dff f003cfff 7007fffe 7817fffe 3ef7efff
  //   1ff7e7ff fff7a3ff fdff33ff d1fb33ff 7fb7ff 10ff37ff 38ff3fff 3bff3fff 3bff3fff bfffbeff 3fffff3f
  //   1fffff1f 9fffff9f 6fffffcf 17*ffffffff 7 407 f000070f fc0070ff fffe0c3f 7bd78f7f fcc5837f 1de3f1ff
  //   e1f3f9ff fc3dffff 70e71fff 1c3ffbf 67fffcff c1fff09f c3ffff7f ffffc7f 3ffcffff ffffffbf 7fffff9f
  //   4*ffffffff fff8003f 4*fffc001f fffc003f fffe003f ffff003f ffff003f 3c000000 e000000 12*0 fffffff0
  //   ffffffdc ffffffe6 fffffff2 3fffff8 fffffffc fffffffe 11*ffffffff 1ff8 7f0 3c0 180 15*0 7 f 1fc00
  //   4*fc00 80fc00 80fe00 90fe00 190fe00 80fe00 80fe00 fe00 9fe00 9fe00 ffe00 7fe00 87e600 c3c000 c00000
  //   0 c00000 c00000 c00000 0 0 0 ff 1f 7 4000 8*0 1c07fff 8000c62 1c860 3f840 7c0c0 fc0c0 1f8080 3f8080
  //   7f8180 ffffffff ffffffff fffffffe fffffffe 7fffffff 11*ffffffff fffffbff fffffbff 4*ffffffff
  //   fffffdff 11*ffffffff ffe7ffff 7*ffffffff fffffff8 fffffffc fffffffe fffffffe ff600000 fffffffe
  //   fffffffe 20*ffffffff 33ffc 33ffc 33ffc 32ffc 32bfc 30bfc 309bc 309bc 5*308bc 309bc 309bc 309bc 30bbc
  //   30bfc 30bfc 30bfc 4*ffffffe0 ffffffe6 fffffffe fffffffe ffffffe4 ffffffe4 ffffffe6 32*ffffffff
  //   fffffff8 fffffff0 fffffff0 ffffffe0 ffffffe0 fffffff0 fffffff0 fffffffc fffffffe 15*ffffffff
  //   d7f70000 d7fc000f d7f0003f c7f0003f e7f0000f e7e0000f e7f0000e e7f00003 e7f80003 e3f80001 f3f88001
  //   f3fe200f f7fe0000 f5fe0000 f9ff03e0 fbfff8f0 fafff87c faffe07e fb7fe07f fbffe03f fafff03f fcffe03f
  //   fc7fc01f fe7fe01f fe7fe00f febfd00f ffbff007 ff5fe807 ff4ff003 ffe7f802 ffb7fc00 ffb3ffff ff92fdc0
  //   fc07e00 7e00 7d80 7c0fff0 ffecf01f ffecf000 ffecf800 ffecff00 ffecff80 ffedff80 ffedff80 ffe9fd00
  //   ffe9fc00 ffe9fc00 7fe000 4*3ff000 3ff800 3ff800 1ff800 41fffe0 41fbbe0 4193be0 101ac0 101a00
  //   20101a00 28001a00 8001a00 8001e00 8000e00 8001800 8001800 181ffc00 5*101ffe00 101fff00 101fff00
  //   901fff00 101fff00 101fff80 101fff80 4*301fff80 fefff3fe fefff1fe fefff1ff feffe3ff feffe3ff feff03ff
  //   fe4003ff 7a0003ff fa5003ff fa7c03ff fa7c03ff fb7c03ff fb7c03fe fb7c03ff fb7c03ff fb7c03ff ff7c03ff
  //   7d3803ff 7d0003ff 7d0003ff fd0003ff fd2003ff ff3003ff ff7807ff ff7c07ff ff7e07ff fffe07ff fffc0fff
  //   fbfc0fff fbfc0fff 1f 1e 1e e c c 1c 3fc 10ffe ffe 71e 400000e 1800000e c00000c c00000c 1800000c
  //   600000c 6*a 18*ffffffff ffffffc0 fffffe00 fffffe00 ffffffdf 33*ffffffff 1c0fce00 1c0fce00 1c0fcc00
  //   3c0fcc00 380f8c00 4*300f8c00 100f8c00 f8c00 f8c00 f8c00 fcc00 fce00 fce00 5*7ce00 0 0 20000 3 f 4*7f
  //   1f 7 1 3 808f 9800f f f 3 7 1f 7f 1ff 3ff 1ff 1ff 1ff ff fe0035ff 38ff 199e e000 ef070 ff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
  //   contents of rom_2 (hex, n*v repeats v):
  //   0 fffffff8 fffffff8 fffffffc 4*ffffffff fffffffe fffffffe 4*ffffffff 7ff9fc ffc fe00007c ffffe07c
  //   11*fffffffc ffffffff ffffffff 0 7ffffff ffffffff 1fffff3c c00 ffffffff ffffffff ffffff47 fffffe02
  //   fffffc00 fffff807 fffff807 fffffc00 ffffffc0 20*ffffffff fffffffe fffffff0 fffffff0 fffffff8
  //   fffffffc 23*ffffffff ffffff8f ffffff9f ffffffff ffffffff fffffc3f ffff803f fffe007f fffc003f
  //   fffe003f ffff003f ffffe01f 7*ffffffff 1ff7 30ffd e1ff 31ff 2001dff dfe 68e 800 8*0 600 1e00 0 0
  //   1f9ff 1fb80 1fb80 1f380 1f380 1f380 1fb00 1ff00 1ff00 1ff00 ffffffe0 fffffff0 fffffff0 ffffffe0
  //   fffffff0 ffffffff ffffffff ffffffff fffbffff 19*ffffffff fffef800 fffdfc02 7ffffe02 7fffff00
  //   ffffff80 ffffffe6 ffffffe7 7ffffffe ffffffff 7fffffff fffffffe ffffffc0 ffffffc0 ffffffe0 ffffffe0
  //   fffffff0 fffffff0 fffffff8 ffffffd8 fffc0000 6*0 78000000 ff800000 fffff6f0 fffffff8 fffffffe
  //   fffffffe fffffffe fffffffc fffffffc fffffffe fffffffe 16*ffffffff fffffff0 fffffff0 fffffffc
  //   16*ffffffff fffff7ff ffffe7ff ffffc7ff ffffcfff ffffcfff fffff3ff ffffffff ffffffff ffffefff
  //   ffffbfff 5*ffffffff fff8ffff fff8ffff ffffffff ffffffff ffffffff fffffff8 fffffffe ffffffff ffffffff
  //   ffffffff ffff3fff ffffffff ffffffff fffff842 ffffffff ffffffff ffffffff 9*0 7e0 64 1fc 7ffe 1fffe
  //   1fffe 1ffa 13f0 6*0 1 7e 1ff 3ff ffff fffff 1f59ffff 3ddb7fe 3fe 7fc 7fe 3fe 1fd 7e 1b 6*0 178 7fc
  //   1ffe bffe bfff bfff 7f42004 3fb0 7f 7f ff 1ff 4*7ff fff 1fff 7fff ffff 1ffff 1ffff ffff 7fff 1fff
  //   7ff ff fffffffe fffffffe fffffffc fffffffe 0 ff000000 fffffffe 17*ffffffff 7fffffff ffffffff
  //   fffffffe f7fffffe 64408183 42c08103 ffffffff ffffffff ffffffff dfffffff ffffff 1fffff 387ffff
  //   3c1ffff 1e1ffff ffff ffff ffff c000ffff c0007fff 80007fff 7dff ffff 1ffff 7ffff fffff 4f7fff ffcfff
  //   1ffdfff 1ff3fff c3fe33ff e187ff e0038fff f0039ffe f03f9ffe f07f8fff 70ffc7ff 40ffdfff 7fdfff 87fdfff
  //   5c7cdfff dffdffff dffdffff cffdffff efffffff 67ffffff 37ffff7f 37ffffff 37ffffbf fffffffe
  //   16*ffffffff 7 3 f f8000f3f f80070ff fffc18ff 7f0f1eff fcc73eff 1de7ffff c086f1ff f87cd87f 60c7ffbf
  //   3ffff7f c1fff1bf fffa7f ffffeff 3ffdfbff 3ffdefff 7fffffbf 4*ffffffff fff8007f 5*fffc003f fffe003f
  //   fffe003f ffff003f 18e02000 3f000000 12*0 ffffffd8 fffffffc fffffffe fffffffa 0 fffffffc fffffffe
  //   7*ffffffff fffffe5f fffffdbf ffffffff ffffffff e001fd0 14*0 3000000 0 0 3 f 1f 1fc00 4*9fc00 1cffc00
  //   1cffe00 1cffe00 1cffe00 1c7fe00 c7e600 7c000 3c000 18000 400000 400000 600000 600000 f00000 380000
  //   bc2000 17efe00 ffff00 7fff00 fff00 cff80 1ff 7f f 3 1 7*0 7ff87a 6001c62 1001cc44 3f840 7f8c0 fc0c0
  //   1f8080 3f8080 7f0180 ffffffff ffffffff ffffffff 7fffffff 7fffffff 29*ffffffff ff87fbff ffff8fff
  //   6*ffffffff fffffffc fffffffe fffffffe fffffff8 0 fffffffe fffffffe 11*ffffffff fffffc7f fffffe7f
  //   7*ffffffff 3803c 3803c 3c03c 3c038 3c039 3c039 8*3c031 4*3c039 3c038 3c038 ffffffff ffffffff
  //   ffffffe7 ffffffe3 6*ffffffe0 31*ffffffff fffffff8 ffffffe0 ffffffe0 ffffffc0 ffffffc0 ffffffe0
  //   ffffffe0 fffffff0 fffffff8 fffffffe 15*ffffffff cff0007c cff000ff dff000ff d7e000ff d7e0007f
  //   ffe0007f fff0007f ebf0100f edfc4003 edfe8003 fdfe8000 f4ff2000 f6ff0000 f6fff6c0 fe7ffcf8 fe7e00fc
  //   fb7c007e fb3c007f fb3c007f fb3e003f fb3f403f ff3ff03f fdfff81f fd7ff81f fe7ff00f fe7ff00f fe3ff007
  //   ff3fe007 ff1ff803 ff9ff003 ff8ff800 ffaffe07 ffe7fbfc ffd3ffe0 ffdbffe0 ffd9fff0 ffe9fdfe ffe9fe01
  //   ffebfe00 ffebfe00 5*ffe3ff00 ffe7fe00 ffe7fd00 7000 7000 387000 3ff800 3ff800 387000 103000 3cc0
  //   4001de0 19a0 1fe0 1ee0 20001a00 1a00 28001800 8001800 817d800 81ffe00 81ffe00 81ffe00 581ffe00
  //   5*101ffe00 101fff00 101fff00 101fff00 901fff00 101fff80 301fff80 301fff80 301fff00 30101f00 30100320
  //   f9ff19f8 f9fe07fc f9ff01fc f9ff03fc f9fe03ff fdff83ff ffffe3ff feffe3ff fe7fe3ff fa4003ff fa4003ff
  //   4*fb4003ff ff6603ff ff7703ff ff7f03ff ff7f03ff ff7f03ff fdff03f8 fdfe03ff fdfe03fe fcfe07ff fdfe07ff
  //   fdfe07ff fdfc07ff f9fc0fff f9fc0fff fbfc0fff 3ffff 3ffff 3ffff 1f 1f e a a a 400000a c00000a
  //   1c000000 400000e 1c00000e c00000e 4*e 4*1000e 17*ffffffff ffffffc0 fffffc00 fffff800 fffff800
  //   fffffe00 ffffffe0 fffffffe 31*ffff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
  //   contents of rom_3 (hex, n*v repeats v):
  //   0 fffffff0 fffffff8 fffffffc fffffffe ffffffff ffffffff fffffffe fffffffc fffffffc 4*ffffffff
  //   fffff07c 3ffff87c 7ffc fc ff80007c fffff07c 9*fffffffc ffffffff ffffff80 7fffffff ffffffff ffffffff
  //   7c00 0 ffffff8f ffffff07 fffffc04 fffff000 ffffe000 ffffe01c fffff01f fffff807 fffffe00 fffffff0
  //   19*ffffffff fffffffc fffffff0 fffffff0 fffffff0 fffffff8 8*ffffffff ffffeffe 13*ffffffff fffffe07
  //   fffffc07 fffffc07 fffffc0f fffff80f ffff8018 fffe003c fffc003f fffc003f fffc003f fffe001f ffff000f
  //   ffff800f 6*ffffffff 6381f 18f9d 67fb 19bc 200019c 3800 19c00 1ee10 8*0 600 1e00 0 0 205ffff 1f39c
  //   1f380 1f380 1fb80 1fb80 4*1ff00 fffff000 fffff800 ffffff00 ffffff00 ffffffc0 ffffffff ffffffff
  //   ffffffff fff3ffff 19*ffffffff fffffe06 7ffffe06 7fffff00 ffffff80 ffffffc6 ffffffe7 7fffffff
  //   ffffffff 7fffffff ffffffff fffffffe ffffffc0 ffffffc0 ffffffe0 fffffff0 fffffff0 ffffff80 d8800000 0
  //   0 ce001c0 fffffff8 11*fffffffe fffffffc fffffffe fffffffe fffffffe 16*ffffffff fffffff0 ffffffe0
  //   fffffffc 16*ffffffff ffffe7ff ffffc7ff ffff87ff ffff8fff ffff9fff ffffe7ff ffffff7f ffffffff
  //   ffffffff ffff8fff 5*ffffffff ffff3fff ffffc9ff fffbffff ffffffff ffffffff fffffff0 fffffffe
  //   6*ffffffff ffffffe0 ffffffff ffffffff ffffffff 9*0 7e0 64 1fe 7ffe fffe fffc ffc 13ac 0 0 0 c0 70 7c
  //   7f 1ff 7ff 7ff 8ffff fffff f0bffff 35b1fff 1ffe 1ffe 1ff6 1ffb 7f8 1ff 7f d 5*0 1dc ffe 3fff bfff
  //   bfff bfff 7f08060 1fff 1ff 3ff 3ff 3ff 4*fff 1fff 1fff 7fff 1ffff 3ffff 3ffff ffff 7fff 3fff fff 3ff
  //   fffffffe fffffffe fffffffc 0 fff00000 fffffffe fffffffe 17*ffffffff 7fffffff fffffffe ffffffff
  //   fffffffb 42810327 3b830fb7 ffffffff ffffffff dfffffff fffffff 3fffff 70fffff 781ffff 3c07cff 3e07cff
  //   1e1ffff e3ffff 1ffff 80007fff 7eff b4ff 7418ff 1c833ff c7ff 3dfff 73fff f3fff f5fff 2fbfff 7ffff
  //   17e7ff c207ff c187ff c38fff 39fff 401f9fff 403f9ffe 403f9fff 6199fff 4e39ffff 6ffdffff 47ffffff
  //   47ffffff f9fffff 3b8dffff 1f8dffff 5f8dffff 5fc6ffff 5fc6ffff fffffffe fffffffe 15*ffffffff 1 5 f
  //   4000083f f8008f7f f000e1ff f09cf1ff 7f1831ff fefdb8ff f9e7beff 7c1de3ff 38087eff 41cffe7f 7ffffff
  //   c1ffeeff 81fffdff 1fff8ff 30ffdfff f9ffcfff 4*ffffffff fff8007f fff8007f fffc003f fffc003f fffc003f
  //   fffc007f fffe007f fffe007f ffff007f e0fc00 1e000000 c7000000 8000000 10000000 0 0 100000 6*0
  //   ffffffdc fffffffe fffffffe 0 fffffff8 fffffffc fffffffe ffffffff ffffffff ffffffff ffffff3f fffffea7
  //   fffffea7 fffffd6f fffffadf fffffd9f fffffdbf ffffffff 1c00001f 11*0 7c0000 7f0000 ff0000 3f00001 1 7
  //   f 1f 3f 78000 78000 38000 38000 0 600000 e00000 e00000 1e00000 e00000 600000 400000 0 0 300000
  //   3c7e00 3ffe00 7fff00 7fff80 1fff80 4*3fff80 1fff80 1fff80 3ff ff 3f f 7 1 7*0 380fffe 8001c44 1d840
  //   7f8c0 7c0c0 f8080 1f8100 3f0100 ffffffff ffffffff ffffffff fffffffe 7fffffff 7fffffff 22*ffffffff
  //   fff8ffff 5*ffffffff ff0ffcff ffffa7ff ffff9fff 5*ffffffff fffffffc fffffffe fffffffa 0 fffffffe
  //   fffffffe fffffffe 9*ffffffff fffff97f fffff97f fffffd3f fffffe3f fffffe3f 4*ffffffff fffffe3f
  //   fffffc7f 3c873 3d873 3d87b 3c87b 8*3d87b 6*3d879 3c879 3c879 ff7fffff 39*ffffffff fffffffc ffffff80
  //   ffffff80 ffffff00 ffffff81 ffffff81 ffffffc1 ffffffc0 ffffffe0 fffffff0 fffffffc fffffffe
  //   14*ffffffff d3f003ff dbf003ff dbf003ff dbf003ff dbf001ff d9f021fe e9f801ff e9fc00ff ec7c4000
  //   e41f8000 6407c000 7401f000 740019ff 760007fe 760000fe 760000fe fe40007f fb40007f fb40007f fb00007f
  //   3b00003f 7900003f fd9f001f fd9ff01f ff9ff80f fedffc0f fedffe07 ff4ffe07 ff5ffe03 ff5ffc03 ff9ff003
  //   ff8ff801 ff8ff87f ffcff9f8 ffc7fdf8 ffc7fcfc ffe7fc07 ffe7fe00 ffe3ff00 ffe3ff00 ffe3fe00 ffebfe00
  //   ffebff00 ffebff00 ffe7fe00 ffe7fd00 ffe7fd30 3fc000 6000 7800 2980 3900 3800 8003880 37c0 1ff9e0
  //   1ffca0 201ffde0 1fffc0 1ffc40 201ffc00 81ffc00 81ffe00 81ffe00 81ffe00 481ffe00 481ffe00 181ffe00
  //   5*101ffe00 101fff00 101fff00 901fff00 901fff00 301ffe00 30100e40 30100740 30100740 301003e0 301c07e2
  //   fbff0003 fbfe01f0 ffff87f9 ffff83f9 fdfe03f9 f9fe03f9 f9fe03ff f9fe03ff f9fe03ff fbff03ff fbff03ff
  //   fbfe03ff fbfe03ff fbfe03fc fbfe03ff fffe03ff fefe03ff fefe03ff fcfe03ff fcfe03ff fcfe03ff fcfe03f8
  //   fcfe03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
  //   contents of rom_4 (hex, n*v repeats v):
  //   0 fffffff0 fffffff0 fffffff8 fffffffe ffffffff ffffffff fffffffe fffffffc fffffff8 4*ffffffff
  //   fffff07c fffff07c 7ffff87c fffffc 1ffc fc 4000007c ff80007c ffc0007c fc00007c fe00007c fe00007c
  //   fe00007c f000007c 7c ffffffff 2 ffffffff ffffffff 3fffff 800 0 fffffc07 fffffc04 fffff008 ffff8000
  //   ffff0000 ffff0070 ffff8078 ffffe01f fffff800 fffffe00 ffffff80 18*ffffffff fffffffc fffffff0
  //   ffffffe0 fffffff0 fffffff8 8*ffffffff ff3841fc 12*ffffffff fffffe0f ffffc007 ffffc007 ffff8007
  //   ffff8006 ffff8000 ffff0000 fffc0000 fff80000 fff80020 fffc0030 fffc0010 fffe0000 ffff0006 ffff801f
  //   ffffc07f fffff80f ffffff8f ffffffff ffffffff 2007 770803 1de003 77880 2807b840 3bc20 3ce10 1c608 8*0
  //   e00 e00 0 0 dffff 1ffff 1fb98 1fb80 1fb80 1ff80 4*1ff00 ffff0000 ffffc000 fffff000 fffffc00 ffffff00
  //   fffffffc ffffffff ff87ffff fff1ffff 19*ffffffff ffffff80 ffffff80 ffffffe6 fffffffe ffffffff
  //   ffffffff ffffffff 7fffffff ffffffff fffffffe fffffffe ffffffc0 ffffffe0 ffffffe0 fffff700 fffc0000 6
  //   80e 7ffffffe ffffcffe ffff9ffe ffff97fe ffff1ffc ffff9ffe 8*fffffffe fffffffc fffffffc fffffffe
  //   fffffffe fffffffe 16*ffffffff ffffffe0 fffffff0 fffffff8 fffffffe 15*ffffffff ffffc3ff ffff87ff
  //   ffff1fff ffff1fff ffff1fff ffffcfff fffff8ff ffffffff ffffffff ffffe7ff ffffbfff ffffffff ffffffff
  //   ffffffff fff83fff ffffc3ff fffff1ff fffffbff ffffffff ffffffff ffffffe0 fffffff0 6*ffffffff fffffffe
  //   ffffffff ffffffff ffffffff c00 c00 600 6*0 7f0 38 1fc 3ffe fffe 1fffe 5fbe 15be 0 300 7c0 3e0 1fc
  //   1ff 3ff 7ff ffe ffc ffff 2fffff 3afffff 1efbfff 3fff 7ff7 7ff2 3ff2 1ffe fff 7ff 3f 4 4*0 1ae fff
  //   3fff bfff bfff bfff 7f483fc 1fff fff 7ff 7ff 7ff fff fff fff 1fff 1fff 3fff ffff 3ffff 7ffff 7ffff
  //   1ffff ffff 7fff 1fff 7ff fffffffe fffffffc 180 ffe00180 fffffffe fffffffe 20*ffffffff fffffffb
  //   47ffffe7 13073fb7 ffffffff ffffffff dfffffff fffffff efffff 61fffff f03ffff 7c1f9ff 7c0f1ff 3e070ff
  //   3e078ff 3e1f8ff 1e1dcff f5dcff f2c07f f0407f 1e0007f 3c000ff 79803ff 7200fff 31fff 73fff fdfff 7cfff
  //   78fff 787ff e403ff c607ff c007ff 408fff 4000dfff 40effff 61ffffe 77dfffff 73ffffff 23efffff 387ffff
  //   1f0bffff 5f08efff 5f88efff 5fc1e7ff dfe1f7ff 5fe5dbff 5fe19bff fffffffe fffffffe 15*ffffffff 1 0 7
  //   3f c00010ff c0001fff c00103ff c001c3ff 6000e1ff ce9f9ff c1c7bfff fc39c3ff 30e8fcff bff9ff 80fff7ff
  //   1fb9ff 801fffff fffff 600fdfff f01f9fff fc7fbfff ffffffff ffffffff fff800ff fff800ff fff8007f
  //   fffc007f fffc007f fffc007f fffe007f fffe007f fffe007f 80001c00 680a000 ff800000 f7000000 18000000 0
  //   0 0 100000 5*0 fffffffc ffffffee fffffffa 0 fffffffe fffffefe fffffffe ffffffff ffffffff fffffebf
  //   fffffda7 fffff9e7 ffffffe7 ffffff47 ffffe6cf ffffe59f ffffff9f ffffffbf c00003f 10000007 5*0
  //   f0000000 18000000 c000000 f800000 1f80000 ff0000 7f8000 3f8001 7c0003 3 1f 1f 3f 7f 4*0 300000
  //   700000 1f80000 1f80000 1fc0000 fc7c00 fffe00 7fe00 fff00 8fff00 bfff00 6*1fff00 3fff00 3fff00 3fff00
  //   1fff00 1fff00 3ff 1ff 7f 1f f 7 7 6*0 fff000 6003c64 1001d8c4 3f0c0 7c080 fc080 1f0100 3f8100
  //   7fffffff ffffffff ffffffff fffffffe 7ffffffe 7fffffff 7fffffff 7*ffffffff ffff7fff ffffffff ffffffff
  //   ffffffff fffff7ff 9*ffffffff fff83fff fffc7fff 4*ffffffff ff1fffff fffba03f ffff0fff 5*ffffffff
  //   fffffffc fffffffe ffffff80 1ffff8 fffffffe fffffffe fffffe7e fffffe3f fffffe0f ffffff17 ffffff9f
  //   ffffff7f ffffffff ffffffff ffffffff fffff9ff fffff93f fffff93f fffff93f fffff83f fffffc1f ffffff3f
  //   ffffff7f ffffff7f fffffe3f fffffe3f fffffc7e d03d8f3 d83d8f3 fc3d8f2 1fe3d8fa 1fe3dcfe 1fe3defe
  //   1fe3defe 4*1fe3dcfe 4*1fe3defe 1fe3dcfe 1fe3dcfe 1fe3dcfe 1fe3defe 1fe3defe fe1fffff 9*ffffffff
  //   fffff800 fffff800 fffffc03 ffffffff ffffffff fffdfc7f ffffe0ff ffffe3ff 14*ffffffff ffffff9f
  //   ffffff87 ffffff87 ffffffff ffffffff ffffffff ffffffbf fffffe08 fffffc00 fffffc00 fffffc01 fffff803
  //   fffffc03 fffffe03 ffffff03 ffffff81 ffffffc0 ffffffe0 fffffff0 fffffffe 14*ffffffff d1f0003f
  //   d1f0003f d8f0003f d8f0001f d9f0001e d8f80000 f9780000 f97e0000 edffc000 edffc000 fdf07006 fcfc19ff
  //   f6fe0dff f6ff00ff fefe00ff fefe00ff fefe007f feff007f faff007f faff007f fb7f003f ff3e003f fd80001f
  //   1d80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
  //   contents of rom_5 (hex, n*v repeats v):
  //   0 ffffffe0 fffffff0 fffffff8 fffffffc ffffffff ffffffff fffffffe fffffff8 fffffff0 ffffffc1 ffffffff
  //   ffffffff ffffffff fffff07c fffff07c fffff07c fffff87c 7ffffffc 1fffffc fffc 1ffc ffc 4*3ffc 7ffc
  //   7fffc ffffff00 ffffffff ffffffff ffffffff 7e00 0 0 ffffc006 ffff800c ffff0000 fffe0000 fffc0080
  //   fffc00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
  //   contents of rom_6 (hex, n*v repeats v):
  //   0 ffffffe0 fffffff0 fffffff8 fffffffc fffffffe fffffffe fffffffc fffffff0 ffffffe7 fffffe00 fffffe03
  //   ffffffbf ffffffff ffffe07e ffffe07e fffff07e fffff07c fffffc7c fffffe7c fffffffc 6*7ffffffc fffffffc
  //   fffffffc 0 ffffffff ffffffff 3ffffff 0 0 0 ffff8000 ffff0018 fffe0000 fffc0000 fff80000 fff80000 f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
  //   contents of rom_7 (hex, n*v repeats v):
  //   0 ffffffc0 ffffffe0 fffffff0 fffffffc fffffffe fffffffc fffffff8 ffffffee fffffff8 ffffc000 ffffc001
  //   ffff8006 ffff001e ffffc07e ffffe07e ffffe07e ffffe07e fffff07c fffff87c fffffc7c fffffc7c fffffc7c
  //   fffff87c fffff9fc 4*fffffffc ffffffff ffffffff ffffffff 7ffff 0 0 0 ffff0018 ffff0010 fffe0000 fffc0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
  //   contents of rom_8 (hex, n*v repeats v):
  //   0 ffe7ffc0 fff0ffe0 fff87ff0 fff11ff8 fff8fffc fff8fffc fffcffff fffc7ff8 fffe0ff8 ffffc000 ffff8000
  //   ffff0000 fffe0000 4*ffffc07e ffffe07e fffff07e fffff07e fffff87e fffff87e fffff07e fffff07c ffffc7fc
  //   ffff9ffe fffffffc fffffffc ffffffff ffffffff 1fffffff 3c00 0 0 0 ffff0030 fffe0000 fffc0000 fff800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
  //   contents of rom_9 (hex, n*v repeats v):
  //   0 bc00ffc0 cf803fc0 ff801fe2 ffe007f3 fff003ff fff007fe fff00ff8 fff803e0 fff800c0 ffffc000 ffff8000
  //   ffff0000 fffe0000 5*ffff807e ffffe07e ffffe03e ffffe03e ffffe07e ffffe07e ffffe07e ffffc6fe ffff1ffe
  //   fffff0fe fffff07e ffffffff ffffffff 7ffe00 4*0 ffff0020 fffe0000 fffc0000 fff80000 fff00000 fff000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
  //   contents of rom_10 (hex, n*v repeats v):
  //   0 7f80 c0003fbf f0000fff fc0007fc fe4001f8 ffd001f8 ffe003e0 ffe00000 fff00000 ffff8000 ffff0000
  //   fffe0000 fdfc0000 ffff007e ffff007e fffe00fe fffe00fe ffff007e ffff807e ffffc03e ffffc03e ffffc07e
  //   ffffc07e ffffc07e ffff80fe ffff0ffe ffffe07e ffffe07e ffffffe0 ffffffc0 30000 4*0 fffe0000 fffe0000
  //   fffc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
  //   contents of rom_11 (hex, n*v repeats v):
  //   0 7f7f 1f81 e0000080 f8000020 fe000000 ff000020 ffc00000 ffc00000 ffe00000 ff7f8080 fe7f0000
  //   fc7e0000 f8fc0000 fffe00ff fffe00ff fffe00fe fffe00fe fffe007e 6*ffff807e ffff80fe ffff0dfe ffffc07e
  //   ffffc07e fffffe00 7fff000 5*0 fffe0000 fffc0000 fff80000 fff00000 ffe00000 ffe00000 f9e00000
  //   f0600000 f810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
  //   contents of rom_12 (hex, n*v repeats v):
  //   0 0 0 c0000000 f0000000 fa000000 fe000000 fe000000 ff000000 ff800000 fe070080 fc070000 f80c0000
  //   f0080000 4*fffe00ff ffff00fe ffff007e ffff007e ffff807e ffff807e ffff007e ffff00fe ffff00fe fffe0dfe
  //   ffff807e ffff807e ffffc000 1e0000 5*0 ffffe000 fffec000 fffd8000 ffb30000 fc700000 f0600000 e0000000
  //   f2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
  //   contents of rom_13 (hex, n*v repeats v):
  //   0 0 0 c0000000 f0000000 f0000000 fc000000 fe000000 ff000000 ff800000 fe01e0c0 fc080400 f8100000
  //   f0000000 ffff00ff ffff00ff fffe00ff fffe00ff ffff00ff ffff007f 4*ffff007e fffe00fe fffe00fe fffc09fe
  //   ffff00fe ffff007e 7ffc0000 6*0 fffc6c00 ff887c03 fe11fa07 f803e80f f8078000 e00e0000 e20e0000
  //   e20e0000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
  //   contents of rom_14 (hex, n*v repeats v):
  //   4*0 e0000000 f0000000 f8000000 f8000000 fe000000 ff000000 fc603000 fc406000 f8c1d000 f1830000
  //   ffff00ff ffff00ff ffff00ff fffe01ff ffff00ff ffff807f 4*ffff007f fffe00ff fffc00ff fff801ff fffe00ff
  //   fffe007f 1e00000 0 80000 4*0 ff987c01 ff18f802 fc28fc06 f849fe0e f289fa1e e609c000 e609c000 e389c000
  //   f3f9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
  //   contents of rom_15 (hex, n*v repeats v):
  //   4*0 80000000 e8000000 f0000000 f0000000 f8000000 fc000000 fc601400 fc782e00 f878c000 f0f18000
  //   ffff80ff ffff00ff ffff01ff fffe01ff ffff00ff ffff80ff ffff007f ffff807f ffff807f ffff00ff ffff00ff
  //   fffc00ff fff800ff fffc00ff fffc007f 0 0 80000 4*0 ff08e000 fe58e000 fc8fc003 f10fc00f f21fd00f
  //   e67ff01f e7f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
  //   contents of rom_16 (hex, n*v repeats v):
  //   0 12 12 12 80000002 e0000000 f0000012 f0000010 f0000000 f8000012 fc181000 fc380000 f8380800 f0780800
  //   ffff80ff ffff01ff ffff01ff fffe03ff ffff01ff 5*ffff80ff ffff00ff fffe00ff fff800ff fffc00ff fffe00ff
  //   0 0 c0000 4*0 fe2fc000 fe7fc000 fcff0000 f1fc0000 f3f80003 e6f8000f f7fc0000 fffe2000 ffff3400 fff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
  //   contents of rom_17 (hex, n*v repeats v):
  //   5*0 c0000000 e0000000 f0000000 f0000000 f8000000 fe08f000 fc18e000 f838f000 f838e000 ffff81ff
  //   ffff01ff fffe01ff fffe03ff fffe03ff ffff80ff ffffc0ff ffffc0ff ffff80ff ffff80ff ffff00ff fffe00ff
  //   fff800ff fffc00ff fffe00ff 0 400000 1c0000 10000 0 0 0 fe3f8000 fe6f0000 fcde0000 f9fc0000 f3fc0000
  //   f3f8000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
  //   contents of rom_18 (hex, n*v repeats v):
  //   0 0 0 1000 400 c0000000 e0000000 e0000000 f0000000 f8000000 fe0fe000 fe1ee000 ff7fc000 ffffc000
  //   ffff81ff ffff01ff fffe03ff fffc03ff fffe03ff ffff81ff ffffc1ff ffffc0ff ffff80ff ffff80ff ffff01ff
  //   fffe01ff fff801ff fffe00ff fffe00ff 0 800000 180000 4*0 ff3f8000 fe3f8000 fc7f0000 fdfe0000 fffc0000
  //   fffc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
  //   contents of rom_19 (hex, n*v repeats v):
  //   0 80 0 0 600 80000000 c0000000 c0000000 e0000000 f0000000 ffff0000 fffe0000 ffff8000 ffff0000
  //   ffff81ff ffff01ff fffe03ff fffc33ff fffe07ff ffff83ff ffffc1ff ffffc1ff ffff81ff ffff83ff ffff03ff
  //   fffe03ff fffc03ff fffe01ff ffff01ff 0 800000 180000 4*0 ff9fc000 ffff8000 ffff0003 ffff070f fffffe0f
  //   fffffe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
  //   contents of rom_20 (hex, n*v repeats v):
  //   0 3e8c0 20 10 400 80000380 c0000000 c0000000 e0000000 f0000000 ffff8000 ffff0000 fffc0000 fff80000
  //   ffff81ff ffff03ff fffe03ff fff837ff fffc07ff ffff83ff ffffc3ff ffffc3ff ffff83ff ffff83ff ffff03ff
  //   fffe03ff fffc03ff fffe03ff ffff01ff 0 0 0 20000 0 0 0 ffffe000 ffffc000 ffff8781 ffffff87 ffffff0f
  //   fff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
  //   contents of rom_21 (hex, n*v repeats v):
  //   0 183ffc3 c12f0 c0018 4 80000380 c00001c0 c0000180 c0000300 e0000100 ffff8000 ffff0000 fffe0000
  //   fffc0000 ffff83ff ffff03ff fffe03ff fff03fff fffc27ff ffff83ff ffffc3ff ffffc3ff ffff83ff ffff03ff
  //   ffff03ff fffe03ff fffc03ff fffe03ff ffff03ff 0 0 4000 30000 0 0 0 fffffffc fffffff8 ffffffe1
  //   ffffffc3 fff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
  //   contents of rom_22 (hex, n*v repeats v):
  //   0 1f1c9e7 38fff3 f00f9 70006 80000302 c00001c0 c00001e0 c00001e0 e00001c0 ffffc000 ffff0000 fffe0003
  //   fffc0007 ffff83ff ffff03ff fffc13ff ff807fff fff83fff ffff87ff ffffc7ff ffffc3ff ffff83ff ffff07ff
  //   ffff07ff fffe07ff fffc07ff fffe07ff ffff07ff 0 1c0000 fc000 18000 0 0 0 fffffffe fffffffc fffffff0 f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
  //   contents of rom_23 (hex, n*v repeats v):
  //   0 1f8e1ef 7c76ff f3fff 7c01f 80038003 c0000381 c00003c1 c00001f0 e00000f8 ffffc000 ffff8000 fffe000f
  //   fffc001f ffff03ff fffe03ff fff01fff ff807fff ffc03fff 4*ffff87ff ffff07ff fffe07ff fffe07ff fffc07ff
  //   ffff07ff ffff07ff 400000 fc0000 7e000 e000 0 0 0 fffffffe fffffffc fffffff8 fffffff3 ffffffe7 ffff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
  //   contents of rom_24 (hex, n*v repeats v):
  //   0 3f8ffff 7c39ff 1f3f7f 7dfff c003e01f c0010003 c0000380 c00191c0 e00088f8 ffffe000 ffff8001
  //   ffff007f fffe0fff fffe03ff fff803ff ffc03fff ffe0ffff ffc07fff ffff07ff ffff87ff ffff87ff ffff07ff
  //   fffe07ff fffe07ff fffe07ff fffc07ff ffff07ff ffff07ff 7000000 7e0000 3f000 f000 10000 0 0 fffffffe
  //   fffffffc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
  //   contents of rom_25 (hex, n*v repeats v):
  //   0 3fbffff fe7ffe 3f1f98 c007cfc0 c001f798 c001f00c c001b104 e0011182 f000d9c1 ffffe000 ffffc01f
  //   ffffffff ffffffff fff807ff fff007ff fff03fff fff9ffff fff8ffff fffe0fff ffff07ff ffff07ff ffff07ff
  //   4*fffc07ff fffe07ff ffff07ff 3000000 3f0000 1f000 7e00 10000 0 0 ffffffff fffffffe fffffff9 fffffff3
  //   ffff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
  //   contents of rom_26 (hex, n*v repeats v):
  //   0 3fffc00 feff00 3f1f80 e00fc7e0 e001f7f8 e001f00c e001f00c e001f10f f000d9c7 ffffff80 ffffffff
  //   ffffffff ffffffff ffff07ff fffc0fff fffe7fff ffffffff ffffffff fffc0fff ffff0fff fffe0fff fffc0fff
  //   fff00fff fff00fff fff00fff fff80fff fffe0fff fffe0fff 1800000 1f0000 f800 7e00 0 0 0 ffffffff
  //   ffffffff ff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
  //   contents of rom_27 (hex, n*v repeats v):
  //   0 1fffc00 ffff80 c03f3fc0 e00fcff0 f003e3f8 e001fbfc e001f3ee f001f80f f800f807 10*ffffffff fffe0fff
  //   fffc0fff fff80fff ffff1fff fffe1fff fffc1fff fffc1fff fffe0fff ffffdfff f00000 f8000 7800 3e00 0 0 0
  //   17*ffffffff ffffff7f fffff03f ffffc07f ffff81ff ffff81ff ffffc0ff fffff87f ffffffff f8000fff e0003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
  //   contents of rom_28 (hex, n*v repeats v):
  //   0 7fe00 ffff80 807fffe0 e00fdff8 f003f7fc f000f1fe f001f9fe f001f9ff f800fdff 19*ffffffff f00000 0 0
  //   3f00 0 100 0 19*ffffffff fffff0ff ffffc1ff ffffc1ff ffffe1ff ffffffff ffffffff fe0013ff e00013fe
  //   cffc 73ff3 1cff8f 18ff9f 8ffcf 3ffcf cfcf 1002c3ff f80001ff ff0000ff ffc0007f fff0003f fffc0cff
  //   35*fff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
  //   contents of rom_29 (hex, n*v repeats v):
  //   0 7fff00 801fffc0 c03fffe0 e01ffff8 f807fffc f801f7fe f000fbfe f800fbff f800fdff 19*ffffffff 0 0 0
  //   e00 0 10000 0 20*ffffffff ffffe1ff ffffe3ff ffffffff ffffffff ffffffff ff03f3ff e4000ff8 3ff1 3fc7
  //   ff3f 7ff3f 3ff9f 19fff 30ffe 800007fe ff0007fc ffff07ff fffec3ff ffffdbff 36*ffffffff 8*0 5*c e e
  //   5*c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
  //   contents of rom_30 (hex, n*v repeats v):
  //   0 bfffff00 e9ffffc0 f0fffff0 f83ffff8 f807fffe f801ffff f801ffff f800ffff fc007fff 19*ffffffff 5*0
  //   10000 0 25*ffffffff fffffffe fe00afff 900027e7 bf9f 3fe7f 27efc 21ffc 261fe0 83f80 f0001ff0 fffc1ffe
  //   39*ffffffff 8*0 c 700000c 300000e 100000e 80000e 6*e c 7ffff00 fffff04 1fffff06 7ffffc00 7ffffc00 7f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
  //   contents of rom_31 (hex, n*v repeats v):
  //   0 ffffff80 ffffffe0 fffffff0 fffffffc fc0ffffe fc03ffff fc01ffff fc00ffff fe007fff 19*ffffffff 7*0
  //   26*ffffffff fffcffff c0027fff 11f7f 1c7ffc 5c7fe0 2c3e00 107f00 7fc0 fef07ff8 40*ffffffff 8*0
  //   780000c 780000c 380000e 3c0000e 1e00006 603006 803806 6 6 e e e 7ffff00 fffff02 7ffffe00 7ffffc00
  //   7ffffe00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
  //   contents of rom_32 (hex, n*v repeats v):
  //   0 ffffff80 ffffffe0 fffffff0 fffffffc ff9ffffe fe87ffff fe83ffff ff01ffff ff00ffff 19*ffffffff 4*0
  //   1e0 0 0 26*ffffffff ffffffe0 fc01ffff 8fffe 20f800 20fc00 ff00 ff80 e181ffe0 fffffffc 40*ffffffff
  //   3de 4*7fe 39e 88 0 7c0000c 7c0000e 3e0000e 3e00006 f80006 781806 1806 4*6 1006 7ffff00 1fffff00
  //   7fffff0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
endmodule
