// Logisim project sound.circ as structural Verilog: 1 circuit, main circuit sound
module sound (
  input  Clk,
  input  Clr,
  input  En,
  output [13:0] data,
  output [6:0] volume,
  output En_2
);

  wire comparator_1_lt, or_1_out;
  wire [15:14] rom_1_data;
  wire [23:0] counter_1_q;

  Counter #(.width(24), .max('hffffff), .ongoal("wrap"), .trigger("rising"), .behavior("new")) counter_1 (
    .Q(counter_1_q), .clk(Clk), .clr(or_1_out));  // open: load, D, count, carry, preset, down
  or or_1 (or_1_out, Clr, comparator_1_lt);
  Comparator #(.width(24), .mode("twosComplement")) comparator_1 (
    .a(24'hc5c), .b(counter_1_q), .lt(comparator_1_lt));  // open: gt, eq
  ROM #(.addrWidth(24), .dataWidth(16), .Select("low")) rom_1 (.addr(counter_1_q), .data({rom_1_data, data}));

  assign En_2 = En;
  assign volume = 7'b0001000;

  // Notes on the sheet:
  //   contents of rom_1 (hex, n*v repeats v):
  //   100*0 36*20b 9*1ee 0 0 9*1b8 0 0 19*188 5*0 50*15d 12*126 12*15d 25*20b 48*1ee 0 9*1b8 0 0 9*188 0 0
  //   22*15d 0 0 87*14a 25*0 35*1b8 0 9*188 0 0 9*15d 0 0 19*14a 5*0 62*126 12*15d 25*1b8 37*19f 25*15d
  //   12*14a 25*126 62*106 25*0 25*106 25*126 9*1b8 0 0 62*1b8 50*0 25*20b 25*1ee 100*188 75*0 25*115
  //   25*126 9*15d 0 0 62*15d 50*0 25*1b8 25*188 37*15d 9*14a 0 0 50*14a 100*0 37*20b 12*1ee 12*1b8 25*188
  //   50*15d 12*126 12*15d 25*20b 50*1ee 12*1b8 12*188 25*15d 87*14a 25*0 37*1b8 12*188 12*15d 25*14a
  //   62*126 12*15d 25*1b8 37*19f 25*15d 12*14a 25*126 62*106 25*0 25*106 25*126 9*1b8 0 0 62*1b8 50*0
  //   25*20b 25*1ee 100*293 75*0 37*293 87*20b 50*0 25*20b 25*24b 100*20b 3300*0 36*20b 9*1ee 0 0 9*1b8 0
  //   0 19*188 5*0 50*15d 12*126 12*15d 25*20b 48*1ee 0 9*1b8 0 0 9*188 0 0 22*15d 0 0 87*14a 25*0 35*1b8
  //   0 9*188 0 0 9*15d 0 0 19*14a 5*0 62*126 12*15d 25*1b8 37*19f 25*15d 12*14a 25*126 62*106 25*0 25*106
  //   25*126 9*1b8 0 0 62*1b8 50*0 25*20b 25*1ee 100*188 75*0 25*115 25*126 9*15d 0 0 62*15d 50*0 25*1b8
  //   25*188 37*15d 9*14a 0 0 50*14a 100*0 37*20b 12*1ee 12*1b8 25*188 50*15d 12*126 12*15d 25*20b 50*1ee
  //   12*1b8 12*188 25*15d 87*14a 25*0 37*1b8 12*188 12*15d 25*14a 62*126 12*15d 25*1b8 37*19f 25*15d
  //   12*14a 25*126 62*106 25*0 25*106 25*126 9*1b8 0 0 62*1b8 50*0 25*20b 25*1ee 100*293 75*0 37*293
  //   87*20b 50*0 25*20b 25*24b 100*20b 100*0 37*20b 12*1ee 12*1b8 25*188 50*15d 12*126 12*15d 25*20b
  //   50*1ee 12*1b8 12*188 25*15d 87*14a 25*0 37*1b8 12*188 12*15d 25*14a 62*126 12*15d 25*1b8 37*19f
  //   25*15d 12*14a 25*126 62*106 25*0 25*106 25*126 9*1b8 0 0 62*1b8 50*0 25*20b 25*1ee 100*293 75*0
  //   37*293 87*20b 50*0 25*20b 25*24b 179*20b 2bba
endmodule
