// Logisim project test.circ as structural Verilog: 1 circuit, main circuit main
module main (
);

  wire button_1_out, clock_1_out, switch_1_p2;
  wire [15:0] rom_1_data;
  wire [23:0] counter_1_q;

  Counter #(.width(24), .max('hffffff), .ongoal("wrap"), .trigger("rising"), .behavior("new")) counter_1 (
    .Q(counter_1_q), .clk(clock_1_out), .clr(button_1_out));  // open: load, D, count, carry, preset, down
  Clock #(.highDuration(1), .lowDuration(1)) clock_1 (.out(clock_1_out));
  Button button_1 (.out(button_1_out));
  ROM #(.addrWidth(24), .dataWidth(16), .Select("low")) rom_1 (.addr(counter_1_q), .data(rom_1_data));
  // Switch #(.width(1)) switch_1: pin names not known; wires that end beside it: 1'b1, switch_1_p2
  // Buzzer #(.freq_measure("Hz"), .vol_width(7)) buzzer_1: pin names not known; wires that end beside it: rom_1_data[13:0], switch_1_p2, 7'b0001000

  // Notes on the sheet:
  //   contents of rom_1 (hex, n*v repeats v):
  //   100*0 80*188 80*14a 178*106 178*dc 178*15d 178*126 267*f7 89*c4 178*188 128*14a 178*106 178*dc
  //   178*15d 178*126 79*f7 79*d0 19*0 89*14a 89*f7 89*c4 149*106 100*dc 200*126 200*f7 100*af 300*14a
  //   200*f7 200*c4 200*106 100*dc 200*126 200*af 200*14a 200*106 100*c4 199*126 99*f7 99*d0 99*a5 100*188
  //   100*14a 200*106 200*dc 179*15d 179*126 267*f7 89*c4 199*188 149*14a 200*106 200*dc 200*15d 200*126
  //   100*f7 100*d0 100*14a 100*f7 100*c4 150*106 100*dc 200*126 200*f7 100*af 300*f7 200*c4 300*14a
  //   200*106 100*dc 200*126 100*f7 100*af 200*106 100*c4 179*14a 79*f7 79*d0 79*a5 3020*0 94*126 132*14a
  //   107*f7 82*d0 58*a5 41*0 80*188 80*14a 178*106 178*dc 178*15d 178*126 267*f7 89*c4 178*188 128*14a
  //   178*106 178*dc 178*15d 178*126 79*f7 79*d0 19*0 89*14a 89*f7 89*c4 149*106 100*dc 200*126 200*f7
  //   100*af 300*14a 200*f7 200*c4 200*106 100*dc 200*126 200*af 200*14a 200*106 100*c4 199*126 99*f7
  //   99*d0 99*a5 100*188 100*14a 200*106 200*dc 179*15d 179*126 267*f7 89*c4 199*188 149*14a 200*106
  //   200*dc 200*15d 200*126 100*f7 100*d0 100*14a 100*f7 100*c4 150*106 100*dc 200*126 200*f7 100*af
  //   300*f7 200*c4 300*14a 200*106 100*dc 200*126 100*f7 100*af 200*106 100*c4 179*14a 79*f7 79*d0 79*a5
  //   20*0 100*188 100*14a 200*106 200*dc 179*15d 179*126 267*f7 89*c4 199*188 149*14a 200*106 200*dc
  //   200*15d 200*126 100*f7 100*d0 100*14a 100*f7 100*c4 150*106 100*dc 200*126 200*f7 100*af 300*f7
  //   200*c4 300*14a 200*106 100*dc 200*126 100*f7 100*af 200*14a 100*106 100*c4 8018
endmodule
