// Logisim project LED.circ as structural Verilog: 1 circuit, main circuit main
module main (
  input  Reset,
  input  Pause
);

  wire Clock_out, or_1_out;
  wire [11:0] counter_1_q;
  wire [31:0] rom_1_data, rom_2_data, rom_3_data, rom_4_data, rom_5_data, rom_6_data, rom_7_data, rom_8_data,
       rom_9_data, rom_10_data, rom_11_data, rom_12_data, rom_13_data, rom_14_data, rom_15_data, rom_16_data,
       rom_17_data, rom_18_data, rom_19_data, rom_20_data, rom_21_data, rom_22_data, rom_23_data,
       rom_24_data, rom_25_data, rom_26_data, rom_27_data, rom_28_data, rom_29_data, rom_30_data,
       rom_31_data, rom_32_data;

  Clock Clock (.out(Clock_out));
  Counter #(.width(12), .max('hc6d)) counter_1 (
    .Q(counter_1_q), .clk(or_1_out), .clr(Reset));  // open: load, D, count, carry
  or or_1 (or_1_out, Clock_out, Pause);
  ROM #(.addrWidth(12), .dataWidth(32)) rom_1 (.addr(counter_1_q), .data(rom_1_data));  // open: sel
  ROM #(.addrWidth(12), .dataWidth(32)) rom_2 (.addr(counter_1_q), .data(rom_2_data));  // open: sel
  ROM #(.addrWidth(12), .dataWidth(32)) rom_3 (.addr(counter_1_q), .data(rom_3_data));  // open: sel
  ROM #(.addrWidth(12), .dataWidth(32)) rom_4 (.addr(counter_1_q), .data(rom_4_data));  // open: sel
  ROM #(.addrWidth(12), .dataWidth(32)) rom_5 (.addr(counter_1_q), .data(rom_5_data));  // open: sel
  ROM #(.addrWidth(12), .dataWidth(32)) rom_6 (.addr(counter_1_q), .data(rom_6_data));  // open: sel
  ROM #(.addrWidth(12), .dataWidth(32)) rom_7 (.addr(counter_1_q), .data(rom_7_data));  // open: sel
  ROM #(.addrWidth(12), .dataWidth(32)) rom_8 (.addr(counter_1_q), .data(rom_8_data));  // open: sel
  ROM #(.addrWidth(12), .dataWidth(32)) rom_9 (.addr(counter_1_q), .data(rom_9_data));  // open: sel
  ROM #(.addrWidth(12), .dataWidth(32)) rom_10 (.addr(counter_1_q), .data(rom_10_data));  // open: sel
  ROM #(.addrWidth(12), .dataWidth(32)) rom_11 (.addr(counter_1_q), .data(rom_11_data));  // open: sel
  ROM #(.addrWidth(12), .dataWidth(32)) rom_12 (.addr(counter_1_q), .data(rom_12_data));  // open: sel
  ROM #(.addrWidth(12), .dataWidth(32)) rom_13 (.addr(counter_1_q), .data(rom_13_data));  // open: sel
  ROM #(.addrWidth(12), .dataWidth(32)) rom_14 (.addr(counter_1_q), .data(rom_14_data));  // open: sel
  ROM #(.addrWidth(12), .dataWidth(32)) rom_15 (.addr(counter_1_q), .data(rom_15_data));  // open: sel
  ROM #(.addrWidth(12), .dataWidth(32)) rom_16 (.addr(counter_1_q), .data(rom_16_data));  // open: sel
  ROM #(.addrWidth(12), .dataWidth(32)) rom_17 (.addr(counter_1_q), .data(rom_17_data));  // open: sel
  ROM #(.addrWidth(12), .dataWidth(32)) rom_18 (.addr(counter_1_q), .data(rom_18_data));  // open: sel
  ROM #(.addrWidth(12), .dataWidth(32)) rom_19 (.addr(counter_1_q), .data(rom_19_data));  // open: sel
  ROM #(.addrWidth(12), .dataWidth(32)) rom_20 (.addr(counter_1_q), .data(rom_20_data));  // open: sel
  ROM #(.addrWidth(12), .dataWidth(32)) rom_21 (.addr(counter_1_q), .data(rom_21_data));  // open: sel
  ROM #(.addrWidth(12), .dataWidth(32)) rom_22 (.addr(counter_1_q), .data(rom_22_data));  // open: sel
  ROM #(.addrWidth(12), .dataWidth(32)) rom_23 (.addr(counter_1_q), .data(rom_23_data));  // open: sel
  ROM #(.addrWidth(12), .dataWidth(32)) rom_24 (.addr(counter_1_q), .data(rom_24_data));  // open: sel
  ROM #(.addrWidth(12), .dataWidth(32)) rom_25 (.addr(counter_1_q), .data(rom_25_data));  // open: sel
  ROM #(.addrWidth(12), .dataWidth(32)) rom_26 (.addr(counter_1_q), .data(rom_26_data));  // open: sel
  ROM #(.addrWidth(12), .dataWidth(32)) rom_27 (.addr(counter_1_q), .data(rom_27_data));  // open: sel
  ROM #(.addrWidth(12), .dataWidth(32)) rom_28 (.addr(counter_1_q), .data(rom_28_data));  // open: sel
  ROM #(.addrWidth(12), .dataWidth(32)) rom_29 (.addr(counter_1_q), .data(rom_29_data));  // open: sel
  ROM #(.addrWidth(12), .dataWidth(32)) rom_30 (.addr(counter_1_q), .data(rom_30_data));  // open: sel
  ROM #(.addrWidth(12), .dataWidth(32)) rom_31 (.addr(counter_1_q), .data(rom_31_data));  // open: sel
  ROM #(.addrWidth(12), .dataWidth(32)) rom_32 (.addr(counter_1_q), .data(rom_32_data));  // open: sel
  DotMatrix #(.matrixcols(32), .matrixrows(32)) dotmatrix_1 (
    .col0(rom_1_data), .col1(rom_2_data), .col2(rom_3_data), .col3(rom_4_data), .col4(rom_5_data),
    .col5(rom_6_data), .col6(rom_7_data), .col7(rom_8_data), .col8(rom_9_data), .col9(rom_10_data),
    .col10(rom_11_data), .col11(rom_12_data), .col12(rom_13_data), .col13(rom_14_data), .col14(rom_15_data),
    .col15(rom_16_data), .col16(rom_17_data), .col17(rom_18_data), .col18(rom_19_data), .col19(rom_20_data),
    .col20(rom_21_data), .col21(rom_22_data), .col22(rom_23_data), .col23(rom_24_data), .col24(rom_25_data),
    .col25(rom_26_data), .col26(rom_27_data), .col27(rom_28_data), .col28(rom_29_data), .col29(rom_30_data),
    .col30(rom_31_data), .col31(rom_32_data));

  // Notes on the sheet:
  //   contents of rom_1 (hex, n*v repeats v):
  //   00000000 fffffff8 fffffffc fffffffe ffffffff ffffffff ffffffff ffffffff fffffffe fffffffe ffffffff
  //   ffffffff ffffffff ffffffff 0000007c fff0007c fffffffc fffffffc fffffffc fffffffc fffffffc fffffffc
  //   fffffffc fffffffc fffffffc fffffffc fffffffc fffffffc fffffffc ffffffff ffffffff fffffffe 78000000
  //   00000000 000007ff 00001c00 ffffffff ffffffff ffffffff ffffffc2 ffffff80 ffffff00 ffffff00 ffffff80
  //   fffffffc ffffffff ffffffff ffffffff ffffffff ffffffff ffffffff ffffffff ffffffff ffffffff ffffffff
  //   ffffffff ffffffff ffffffff ffffffff ffffffff ffffffff ffffffff ffffffff ffffffff ffffffff ffffffff
  //   fffffff8 fffffff8 fffffff8 fffffffc ffffffff ffffffff ffffffff ffffffff ffffffff ffffffff ffffffff
  //   ffffffff ffffffff ffffffff ffffffff ffffffff ffffffff ffffffff ffffffff ffffffff ffffffff ffffffff
  //   ffffffff ffffffff ffffffff ffffffff ffffffff ffffffff ffffffff ffffffff ffffffff ffffffff fffffeff
  //   ffffc07f ffffc07f ffffe03f fffff03f ffffff7f ffffffff ffffffff ffffffff ffffffff ffffffff ffffffff
  //   ffffffff 00000ff7 000007fc 000000ff 0000007f 0a80147f 0000107f 00000c7f 0000067f 00000000 00000000
  //   00000000 00000000 00000000 00000000 00000000 00000000 00000100 00000700 00000100 00000000 0001f18c
  //   0001f180 0001f380 0001f380 0001f380 0001f380 0003f300 0003f700 0003f700 0003ff00 fffffffe ffffffff
  //   ffffffff fffffffc fffffffe ffffffff ffffffff ffffffff ffffffff ffffffff ffffffff ffffffff ffffffff
  //   ffffffff ffffffff ffffffff ffffffff ffffffff ffffffff ffffffff ffffffff ffffffff ffffffff ffffffff
  //   ffffffff ffffffff ffffffff ffffffff f7fcf800 fffdf800 7ffffe00 7ffffe00 ffffff00 ffffffc2 ffffffc7
  //   ffffffe4 ffffffff 7fffffff ffffffff ffffff80 ffffffc0 ffffffc0 ffffffe0 ffffffe0 fffffff0 fffffff0
  //   fffffff8 fffffffc fffffffc ffffffec 7fffffc0 00000000 00000000 00000000 00000000 00000000 00000000
  //   00000000 60000000 fffffffe fffffffe fffffffe fffffffe fffffffe fffffffe ffffffff ffffffff ffffffff
  //   ffffffff ffffffff ffffffff ffffffff ffffffff ffffffff ffffffff ffffffff ffffffff ffffffff ffffffff
  //   ffffffff ffffffff ffffffe0 fffffff0 fffffffc ffffefff ffffffff ffffffff ffffffff ffffffff ffffffff
  //   ffffffff ffffffff ffffffff ffffffff ffffffff ffffffff ffffffff ffffffff ffffffff ffffffff ffffffff
  //   ffffe7ff ffffe7ff ffffcfff ffffe7ff fffff9ff ffffffff ffffffff ffff8fff ffffffff ffffffff ffffffff
  //   ffffffff ffffffff ffffffff ffffffff fff9ffff ffffffff ffffffff ffffffff fffffffe ffffffff ffffffff
  //   ffffffff ffffffff fffe1fff ffffffff ffffffff fffff0ff ffffffff ffffffff ffffffff 00000000 00000000
  //   00000000 00000000 00000000 00000000 00000000 00000000 00000000 000003ec 0000002c 000001fe 00005ffe
  //   0000fffe 0000fffe 000017f4 000017f0 00000000 00000000 00000000 00000000 00000000 00000000 00000000
  //   00000000 0000007e 000000ff 0001ffff 001fffff 17f9fffe 03f97ffc 00000070 000000f8 000001f8 000000fe
  //   0000007e 00000011 00000000 00000000 00000000 00000000 00000000 00000000 00000000 000001b0 000007ff
  //   00003fff 00007ffc 00003ffe 00003ffe 07d88146 00101fc6 00000006 0000001f 0000003f 000000ff 000003ff
  //   000003ff 000003ff 000003ff 000007ff 00000fff 00003fff 0000ffff 0001ffff 0000ffff 00007fff 00003fff
  //   00000fff 000001ff 00000007 ffffffee fffffffe fffffffc fffffffe fffffffe 00000000 ffe00000 ffffffff
  //   ffffffff ffffffff ffffffff ffffffff ffffffff ffffffff ffffffff ffffffff ffffffff ffffffff ffffffff
  //   ffffffff ffffffff ffffffff ffffffff ffffffff 7fffffff 7fffffff fffffffe fffffffe 31fffffa 20604081
  //   ffffffff ffffffff fffffeff ffffffff 8fffffff 007fffff 0003ffff 0002ffff 0001ffff 8005ffff 800dffff
  //   400fffff c006ffff e0037fff c001ffff 8000f8ff 0001ffff 00077fff 002fffff 00efffff 0fffffff 1ffdf7ff
  //   8fffbfff cfffbfff fffe9dff f003cfff 7007fffe 7817fffe 3ef7efff 1ff7e7ff fff7a3ff fdff33ff d1fb33ff
  //   007fb7ff 10ff37ff 38ff3fff 3bff3fff 3bff3fff bfffbeff 3fffff3f 1fffff1f 9fffff9f 6fffffcf ffffffff
  //   ffffffff ffffffff ffffffff ffffffff ffffffff ffffffff ffffffff ffffffff ffffffff ffffffff ffffffff
  //   ffffffff ffffffff ffffffff ffffffff ffffffff 00000007 00000407 f000070f fc0070ff fffe0c3f 7bd78f7f
  //   fcc5837f 1de3f1ff e1f3f9ff fc3dffff 70e7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
  //   contents of rom_2 (hex, n*v repeats v):
  //   00000000 fffffff8 fffffff8 fffffffc ffffffff ffffffff ffffffff ffffffff fffffffe fffffffe ffffffff
  //   ffffffff ffffffff ffffffff 007ff9fc 00000ffc fe00007c ffffe07c fffffffc fffffffc fffffffc fffffffc
  //   fffffffc fffffffc fffffffc fffffffc fffffffc fffffffc fffffffc ffffffff ffffffff 00000000 07ffffff
  //   ffffffff 1fffff3c 00000c00 ffffffff ffffffff ffffff47 fffffe02 fffffc00 fffff807 fffff807 fffffc00
  //   ffffffc0 ffffffff ffffffff ffffffff ffffffff ffffffff ffffffff ffffffff ffffffff ffffffff ffffffff
  //   ffffffff ffffffff ffffffff ffffffff ffffffff ffffffff ffffffff ffffffff ffffffff ffffffff fffffffe
  //   fffffff0 fffffff0 fffffff8 fffffffc ffffffff ffffffff ffffffff ffffffff ffffffff ffffffff ffffffff
  //   ffffffff ffffffff ffffffff ffffffff ffffffff ffffffff ffffffff ffffffff ffffffff ffffffff ffffffff
  //   ffffffff ffffffff ffffffff ffffffff ffffffff ffffff8f ffffff9f ffffffff ffffffff fffffc3f ffff803f
  //   fffe007f fffc003f fffe003f ffff003f ffffe01f ffffffff ffffffff ffffffff ffffffff ffffffff ffffffff
  //   ffffffff 00001ff7 00030ffd 0000e1ff 000031ff 02001dff 00000dfe 0000068e 00000800 00000000 00000000
  //   00000000 00000000 00000000 00000000 00000000 00000000 00000600 00001e00 00000000 00000000 0001f9ff
  //   0001fb80 0001fb80 0001f380 0001f380 0001f380 0001fb00 0001ff00 0001ff00 0001ff00 ffffffe0 fffffff0
  //   fffffff0 ffffffe0 fffffff0 ffffffff ffffffff ffffffff fffbffff ffffffff ffffffff ffffffff ffffffff
  //   ffffffff ffffffff ffffffff ffffffff ffffffff ffffffff ffffffff ffffffff ffffffff ffffffff ffffffff
  //   ffffffff ffffffff ffffffff ffffffff fffef800 fffdfc02 7ffffe02 7fffff00 ffffff80 ffffffe6 ffffffe7
  //   7ffffffe ffffffff 7fffffff fffffffe ffffffc0 ffffffc0 ffffffe0 ffffffe0 fffffff0 fffffff0 fffffff8
  //   ffffffd8 fffc0000 00000000 00000000 00000000 00000000 00000000 00000000 78000000 ff800000 fffff6f0
  //   fffffff8 fffffffe fffffffe fffffffe fffffffc fffffffc fffffffe fffffffe ffffffff ffffffff ffffffff
  //   ffffffff ffffffff ffffffff ffffffff ffffffff ffffffff ffffffff ffffffff ffffffff ffffffff ffffffff
  //   ffffffff ffffffff fffffff0 fffffff0 fffffffc ffffffff ffffffff ffffffff ffffffff ffffffff ffffffff
  //   ffffffff ffffffff ffffffff ffffffff ffffffff ffffffff ffffffff ffffffff ffffffff ffffffff fffff7ff
  //   ffffe7ff ffffc7ff ffffcfff ffffcfff fffff3ff ffffffff ffffffff ffffefff ffffbfff ffffffff ffffffff
  //   ffffffff ffffffff ffffffff fff8ffff fff8ffff ffffffff ffffffff ffffffff fffffff8 fffffffe ffffffff
  //   ffffffff ffffffff ffff3fff ffffffff ffffffff fffff842 ffffffff ffffffff ffffffff 00000000 00000000
  //   00000000 00000000 00000000 00000000 00000000 00000000 00000000 000007e0 00000064 000001fc 00007ffe
  //   0001fffe 0001fffe 00001ffa 000013f0 00000000 00000000 00000000 00000000 00000000 00000000 00000001
  //   0000007e 000001ff 000003ff 0000ffff 000fffff 1f59ffff 03ddb7fe 000003fe 000007fc 000007fe 000003fe
  //   000001fd 0000007e 0000001b 00000000 00000000 00000000 00000000 00000000 00000000 00000178 000007fc
  //   00001ffe 0000bffe 0000bfff 0000bfff 07f42004 00003fb0 0000007f 0000007f 000000ff 000001ff 000007ff
  //   000007ff 000007ff 000007ff 00000fff 00001fff 00007fff 0000ffff 0001ffff 0001ffff 0000ffff 00007fff
  //   00001fff 000007ff 000000ff fffffffe fffffffe fffffffc fffffffe 00000000 ff000000 fffffffe ffffffff
  //   ffffffff ffffffff ffffffff ffffffff ffffffff ffffffff ffffffff ffffffff ffffffff ffffffff ffffffff
  //   ffffffff ffffffff ffffffff ffffffff ffffffff 7fffffff ffffffff fffffffe f7fffffe 64408183 42c08103
  //   ffffffff ffffffff ffffffff dfffffff 00ffffff 001fffff 0387ffff 03c1ffff 01e1ffff 0000ffff 0000ffff
  //   0000ffff c000ffff c0007fff 80007fff 00007dff 0000ffff 0001ffff 0007ffff 000fffff 004f7fff 00ffcfff
  //   01ffdfff 01ff3fff c3fe33ff 00e187ff e0038fff f0039ffe f03f9ffe f07f8fff 70ffc7ff 40ffdfff 007fdfff
  //   087fdfff 5c7cdfff dffdffff dffdffff cffdffff efffffff 67ffffff 37ffff7f 37ffffff 37ffffbf fffffffe
  //   ffffffff ffffffff ffffffff ffffffff ffffffff ffffffff ffffffff ffffffff ffffffff ffffffff ffffffff
  //   ffffffff ffffffff ffffffff ffffffff ffffffff 00000007 00000003 0000000f f8000f3f f80070ff fffc18ff
  //   7f0f1eff fcc73eff 1de7ffff c086f1ff f87c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
  //   contents of rom_3 (hex, n*v repeats v):
  //   00000000 fffffff0 fffffff8 fffffffc fffffffe ffffffff ffffffff fffffffe fffffffc fffffffc ffffffff
  //   ffffffff ffffffff ffffffff fffff07c 3ffff87c 00007ffc 000000fc ff80007c fffff07c fffffffc fffffffc
  //   fffffffc fffffffc fffffffc fffffffc fffffffc fffffffc fffffffc ffffffff ffffff80 7fffffff ffffffff
  //   ffffffff 00007c00 00000000 ffffff8f ffffff07 fffffc04 fffff000 ffffe000 ffffe01c fffff01f fffff807
  //   fffffe00 fffffff0 ffffffff ffffffff ffffffff ffffffff ffffffff ffffffff ffffffff ffffffff ffffffff
  //   ffffffff ffffffff ffffffff ffffffff ffffffff ffffffff ffffffff ffffffff ffffffff ffffffff fffffffc
  //   fffffff0 fffffff0 fffffff0 fffffff8 ffffffff ffffffff ffffffff ffffffff ffffffff ffffffff ffffffff
  //   ffffffff ffffeffe ffffffff ffffffff ffffffff ffffffff ffffffff ffffffff ffffffff ffffffff ffffffff
  //   ffffffff ffffffff ffffffff ffffffff fffffe07 fffffc07 fffffc07 fffffc0f fffff80f ffff8018 fffe003c
  //   fffc003f fffc003f fffc003f fffe001f ffff000f ffff800f ffffffff ffffffff ffffffff ffffffff ffffffff
  //   ffffffff 0006381f 00018f9d 000067fb 000019bc 0200019c 00003800 00019c00 0001ee10 00000000 00000000
  //   00000000 00000000 00000000 00000000 00000000 00000000 00000600 00001e00 00000000 00000000 0205ffff
  //   0001f39c 0001f380 0001f380 0001fb80 0001fb80 0001ff00 0001ff00 0001ff00 0001ff00 fffff000 fffff800
  //   ffffff00 ffffff00 ffffffc0 ffffffff ffffffff ffffffff fff3ffff ffffffff ffffffff ffffffff ffffffff
  //   ffffffff ffffffff ffffffff ffffffff ffffffff ffffffff ffffffff ffffffff ffffffff ffffffff ffffffff
  //   ffffffff ffffffff ffffffff ffffffff fffffe06 7ffffe06 7fffff00 ffffff80 ffffffc6 ffffffe7 7fffffff
  //   ffffffff 7fffffff ffffffff fffffffe ffffffc0 ffffffc0 ffffffe0 fffffff0 fffffff0 ffffff80 d8800000
  //   00000000 00000000 0ce001c0 fffffff8 fffffffe fffffffe fffffffe fffffffe fffffffe fffffffe fffffffe
  //   fffffffe fffffffe fffffffe fffffffe fffffffc fffffffe fffffffe fffffffe ffffffff ffffffff ffffffff
  //   ffffffff ffffffff ffffffff ffffffff ffffffff ffffffff ffffffff ffffffff ffffffff ffffffff ffffffff
  //   ffffffff ffffffff fffffff0 ffffffe0 fffffffc ffffffff ffffffff ffffffff ffffffff ffffffff ffffffff
  //   ffffffff ffffffff ffffffff ffffffff ffffffff ffffffff ffffffff ffffffff ffffffff ffffffff ffffe7ff
  //   ffffc7ff ffff87ff ffff8fff ffff9fff ffffe7ff ffffff7f ffffffff ffffffff ffff8fff ffffffff ffffffff
  //   ffffffff ffffffff ffffffff ffff3fff ffffc9ff fffbffff ffffffff ffffffff fffffff0 fffffffe ffffffff
  //   ffffffff ffffffff ffffffff ffffffff ffffffff ffffffe0 ffffffff ffffffff ffffffff 00000000 00000000
  //   00000000 00000000 00000000 00000000 00000000 00000000 00000000 000007e0 00000064 000001fe 00007ffe
  //   0000fffe 0000fffc 00000ffc 000013ac 00000000 00000000 00000000 000000c0 00000070 0000007c 0000007f
  //   000001ff 000007ff 000007ff 0008ffff 000fffff 0f0bffff 035b1fff 00001ffe 00001ffe 00001ff6 00001ffb
  //   000007f8 000001ff 0000007f 0000000d 00000000 00000000 00000000 00000000 00000000 000001dc 00000ffe
  //   00003fff 0000bfff 0000bfff 0000bfff 07f08060 00001fff 000001ff 000003ff 000003ff 000003ff 00000fff
  //   00000fff 00000fff 00000fff 00001fff 00001fff 00007fff 0001ffff 0003ffff 0003ffff 0000ffff 00007fff
  //   00003fff 00000fff 000003ff fffffffe fffffffe fffffffc 00000000 fff00000 fffffffe fffffffe ffffffff
  //   ffffffff ffffffff ffffffff ffffffff ffffffff ffffffff ffffffff ffffffff ffffffff ffffffff ffffffff
  //   ffffffff ffffffff ffffffff ffffffff ffffffff 7fffffff fffffffe ffffffff fffffffb 42810327 3b830fb7
  //   ffffffff ffffffff dfffffff 0fffffff 003fffff 070fffff 0781ffff 03c07cff 03e07cff 01e1ffff 00e3ffff
  //   0001ffff 80007fff 00007eff 0000b4ff 007418ff 01c833ff 0000c7ff 0003dfff 00073fff 000f3fff 000f5fff
  //   002fbfff 0007ffff 0017e7ff 00c207ff 00c187ff 00c38fff 00039fff 401f9fff 403f9ffe 403f9fff 06199fff
  //   4e39ffff 6ffdffff 47ffffff 47ffffff 0f9fffff 3b8dffff 1f8dffff 5f8dffff 5fc6ffff 5fc6ffff fffffffe
  //   fffffffe ffffffff ffffffff ffffffff ffffffff ffffffff ffffffff ffffffff ffffffff ffffffff ffffffff
  //   ffffffff ffffffff ffffffff ffffffff ffffffff 00000001 00000005 0000000f 4000083f f8008f7f f000e1ff
  //   f09cf1ff 7f1831ff fefdb8ff f9e7beff 7c1d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
  //   contents of rom_4 (hex, n*v repeats v):
  //   00000000 fffffff0 fffffff0 fffffff8 fffffffe ffffffff ffffffff fffffffe fffffffc fffffff8 ffffffff
  //   ffffffff ffffffff ffffffff fffff07c fffff07c 7ffff87c 00fffffc 00001ffc 000000fc 4000007c ff80007c
  //   ffc0007c fc00007c fe00007c fe00007c fe00007c f000007c 0000007c ffffffff 00000002 ffffffff ffffffff
  //   003fffff 00000800 00000000 fffffc07 fffffc04 fffff008 ffff8000 ffff0000 ffff0070 ffff8078 ffffe01f
  //   fffff800 fffffe00 ffffff80 ffffffff ffffffff ffffffff ffffffff ffffffff ffffffff ffffffff ffffffff
  //   ffffffff ffffffff ffffffff ffffffff ffffffff ffffffff ffffffff ffffffff ffffffff ffffffff fffffffc
  //   fffffff0 ffffffe0 fffffff0 fffffff8 ffffffff ffffffff ffffffff ffffffff ffffffff ffffffff ffffffff
  //   ffffffff ff3841fc ffffffff ffffffff ffffffff ffffffff ffffffff ffffffff ffffffff ffffffff ffffffff
  //   ffffffff ffffffff ffffffff fffffe0f ffffc007 ffffc007 ffff8007 ffff8006 ffff8000 ffff0000 fffc0000
  //   fff80000 fff80020 fffc0030 fffc0010 fffe0000 ffff0006 ffff801f ffffc07f fffff80f ffffff8f ffffffff
  //   ffffffff 00002007 00770803 001de003 00077880 2807b840 0003bc20 0003ce10 0001c608 00000000 00000000
  //   00000000 00000000 00000000 00000000 00000000 00000000 00000e00 00000e00 00000000 00000000 000dffff
  //   0001ffff 0001fb98 0001fb80 0001fb80 0001ff80 0001ff00 0001ff00 0001ff00 0001ff00 ffff0000 ffffc000
  //   fffff000 fffffc00 ffffff00 fffffffc ffffffff ff87ffff fff1ffff ffffffff ffffffff ffffffff ffffffff
  //   ffffffff ffffffff ffffffff ffffffff ffffffff ffffffff ffffffff ffffffff ffffffff ffffffff ffffffff
  //   ffffffff ffffffff ffffffff ffffffff ffffff80 ffffff80 ffffffe6 fffffffe ffffffff ffffffff ffffffff
  //   7fffffff ffffffff fffffffe fffffffe ffffffc0 ffffffe0 ffffffe0 fffff700 fffc0000 00000006 0000080e
  //   7ffffffe ffffcffe ffff9ffe ffff97fe ffff1ffc ffff9ffe fffffffe fffffffe fffffffe fffffffe fffffffe
  //   fffffffe fffffffe fffffffe fffffffc fffffffc fffffffe fffffffe fffffffe ffffffff ffffffff ffffffff
  //   ffffffff ffffffff ffffffff ffffffff ffffffff ffffffff ffffffff ffffffff ffffffff ffffffff ffffffff
  //   ffffffff ffffffff ffffffe0 fffffff0 fffffff8 fffffffe ffffffff ffffffff ffffffff ffffffff ffffffff
  //   ffffffff ffffffff ffffffff ffffffff ffffffff ffffffff ffffffff ffffffff ffffffff ffffffff ffffc3ff
  //   ffff87ff ffff1fff ffff1fff ffff1fff ffffcfff fffff8ff ffffffff ffffffff ffffe7ff ffffbfff ffffffff
  //   ffffffff ffffffff fff83fff ffffc3ff fffff1ff fffffbff ffffffff ffffffff ffffffe0 fffffff0 ffffffff
  //   ffffffff ffffffff ffffffff ffffffff ffffffff fffffffe ffffffff ffffffff ffffffff 00000c00 00000c00
  //   00000600 00000000 00000000 00000000 00000000 00000000 00000000 000007f0 00000038 000001fc 00003ffe
  //   0000fffe 0001fffe 00005fbe 000015be 00000000 00000300 000007c0 000003e0 000001fc 000001ff 000003ff
  //   000007ff 00000ffe 00000ffc 0000ffff 002fffff 03afffff 01efbfff 00003fff 00007ff7 00007ff2 00003ff2
  //   00001ffe 00000fff 000007ff 0000003f 00000004 00000000 00000000 00000000 00000000 000001ae 00000fff
  //   00003fff 0000bfff 0000bfff 0000bfff 07f483fc 00001fff 00000fff 000007ff 000007ff 000007ff 00000fff
  //   00000fff 00000fff 00001fff 00001fff 00003fff 0000ffff 0003ffff 0007ffff 0007ffff 0001ffff 0000ffff
  //   00007fff 00001fff 000007ff fffffffe fffffffc 00000180 ffe00180 fffffffe fffffffe ffffffff ffffffff
  //   ffffffff ffffffff ffffffff ffffffff ffffffff ffffffff ffffffff ffffffff ffffffff ffffffff ffffffff
  //   ffffffff ffffffff ffffffff ffffffff ffffffff ffffffff ffffffff fffffffb 47ffffe7 13073fb7 ffffffff
  //   ffffffff dfffffff 0fffffff 00efffff 061fffff 0f03ffff 07c1f9ff 07c0f1ff 03e070ff 03e078ff 03e1f8ff
  //   01e1dcff 00f5dcff 00f2c07f 00f0407f 01e0007f 03c000ff 079803ff 07200fff 00031fff 00073fff 000fdfff
  //   0007cfff 00078fff 000787ff 00e403ff 00c607ff 00c007ff 00408fff 4000dfff 040effff 061ffffe 77dfffff
  //   73ffffff 23efffff 0387ffff 1f0bffff 5f08efff 5f88efff 5fc1e7ff dfe1f7ff 5fe5dbff 5fe19bff fffffffe
  //   fffffffe ffffffff ffffffff ffffffff ffffffff ffffffff ffffffff ffffffff ffffffff ffffffff ffffffff
  //   ffffffff ffffffff ffffffff ffffffff ffffffff 00000001 00000000 00000007 0000003f c00010ff c0001fff
  //   c00103ff c001c3ff 6000e1ff 0ce9f9ff c1c7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
  //   contents of rom_5 (hex, n*v repeats v):
  //   00000000 ffffffe0 fffffff0 fffffff8 fffffffc ffffffff ffffffff fffffffe fffffff8 fffffff0 ffffffc1
  //   ffffffff ffffffff ffffffff fffff07c fffff07c fffff07c fffff87c 7ffffffc 01fffffc 0000fffc 00001ffc
  //   00000ffc 00003ffc 00003ffc 00003ffc 00003ffc 00007ffc 0007fffc ffffff00 ffffffff ffffffff ffffffff
  //   000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
  //   contents of rom_6 (hex, n*v repeats v):
  //   00000000 ffffffe0 fffffff0 fffffff8 fffffffc fffffffe fffffffe fffffffc fffffff0 ffffffe7 fffffe00
  //   fffffe03 ffffffbf ffffffff ffffe07e ffffe07e fffff07e fffff07c fffffc7c fffffe7c fffffffc 7ffffffc
  //   7ffffffc 7ffffffc 7ffffffc 7ffffffc 7ffffffc fffffffc fffffffc 00000000 ffffffff ffffffff 03ffffff
  //   000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
  //   contents of rom_7 (hex, n*v repeats v):
  //   00000000 ffffffc0 ffffffe0 fffffff0 fffffffc fffffffe fffffffc fffffff8 ffffffee fffffff8 ffffc000
  //   ffffc001 ffff8006 ffff001e ffffc07e ffffe07e ffffe07e ffffe07e fffff07c fffff87c fffffc7c fffffc7c
  //   fffffc7c fffff87c fffff9fc fffffffc fffffffc fffffffc fffffffc ffffffff ffffffff ffffffff 0007ffff
  //   000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
  //   contents of rom_8 (hex, n*v repeats v):
  //   00000000 ffe7ffc0 fff0ffe0 fff87ff0 fff11ff8 fff8fffc fff8fffc fffcffff fffc7ff8 fffe0ff8 ffffc000
  //   ffff8000 ffff0000 fffe0000 ffffc07e ffffc07e ffffc07e ffffc07e ffffe07e fffff07e fffff07e fffff87e
  //   fffff87e fffff07e fffff07c ffffc7fc ffff9ffe fffffffc fffffffc ffffffff ffffffff 1fffffff 00003c00
  //   000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
  //   contents of rom_9 (hex, n*v repeats v):
  //   00000000 bc00ffc0 cf803fc0 ff801fe2 ffe007f3 fff003ff fff007fe fff00ff8 fff803e0 fff800c0 ffffc000
  //   ffff8000 ffff0000 fffe0000 ffff807e ffff807e ffff807e ffff807e ffff807e ffffe07e ffffe03e ffffe03e
  //   ffffe07e ffffe07e ffffe07e ffffc6fe ffff1ffe fffff0fe fffff07e ffffffff ffffffff 007ffe00 00000000
  //   000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
  //   contents of rom_10 (hex, n*v repeats v):
  //   00000000 00007f80 c0003fbf f0000fff fc0007fc fe4001f8 ffd001f8 ffe003e0 ffe00000 fff00000 ffff8000
  //   ffff0000 fffe0000 fdfc0000 ffff007e ffff007e fffe00fe fffe00fe ffff007e ffff807e ffffc03e ffffc03e
  //   ffffc07e ffffc07e ffffc07e ffff80fe ffff0ffe ffffe07e ffffe07e ffffffe0 ffffffc0 00030000 00000000
  //   000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
  //   contents of rom_11 (hex, n*v repeats v):
  //   00000000 00007f7f 00001f81 e0000080 f8000020 fe000000 ff000020 ffc00000 ffc00000 ffe00000 ff7f8080
  //   fe7f0000 fc7e0000 f8fc0000 fffe00ff fffe00ff fffe00fe fffe00fe fffe007e ffff807e ffff807e ffff807e
  //   ffff807e ffff807e ffff807e ffff80fe ffff0dfe ffffc07e ffffc07e fffffe00 07fff000 00000000 00000000
  //   000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
  //   contents of rom_12 (hex, n*v repeats v):
  //   00000000 00000000 00000000 c0000000 f0000000 fa000000 fe000000 fe000000 ff000000 ff800000 fe070080
  //   fc070000 f80c0000 f0080000 fffe00ff fffe00ff fffe00ff fffe00ff ffff00fe ffff007e ffff007e ffff807e
  //   ffff807e ffff007e ffff00fe ffff00fe fffe0dfe ffff807e ffff807e ffffc000 001e0000 00000000 00000000
  //   000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
  //   contents of rom_13 (hex, n*v repeats v):
  //   00000000 00000000 00000000 c0000000 f0000000 f0000000 fc000000 fe000000 ff000000 ff800000 fe01e0c0
  //   fc080400 f8100000 f0000000 ffff00ff ffff00ff fffe00ff fffe00ff ffff00ff ffff007f ffff007e ffff007e
  //   ffff007e ffff007e fffe00fe fffe00fe fffc09fe ffff00fe ffff007e 7ffc0000 00000000 00000000 00000000
  //   000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
  //   contents of rom_14 (hex, n*v repeats v):
  //   00000000 00000000 00000000 00000000 e0000000 f0000000 f8000000 f8000000 fe000000 ff000000 fc603000
  //   fc406000 f8c1d000 f1830000 ffff00ff ffff00ff ffff00ff fffe01ff ffff00ff ffff807f ffff007f ffff007f
  //   ffff007f ffff007f fffe00ff fffc00ff fff801ff fffe00ff fffe007f 01e00000 00000000 00080000 00000000
  //   000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
  //   contents of rom_15 (hex, n*v repeats v):
  //   00000000 00000000 00000000 00000000 80000000 e8000000 f0000000 f0000000 f8000000 fc000000 fc601400
  //   fc782e00 f878c000 f0f18000 ffff80ff ffff00ff ffff01ff fffe01ff ffff00ff ffff80ff ffff007f ffff807f
  //   ffff807f ffff00ff ffff00ff fffc00ff fff800ff fffc00ff fffc007f 00000000 00000000 00080000 00000000
  //   000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
  //   contents of rom_16 (hex, n*v repeats v):
  //   00000000 00000012 00000012 00000012 80000002 e0000000 f0000012 f0000010 f0000000 f8000012 fc181000
  //   fc380000 f8380800 f0780800 ffff80ff ffff01ff ffff01ff fffe03ff ffff01ff ffff80ff ffff80ff ffff80ff
  //   ffff80ff ffff80ff ffff00ff fffe00ff fff800ff fffc00ff fffe00ff 00000000 00000000 000c0000 00000000
  //   000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
  //   contents of rom_17 (hex, n*v repeats v):
  //   00000000 00000000 00000000 00000000 00000000 c0000000 e0000000 f0000000 f0000000 f8000000 fe08f000
  //   fc18e000 f838f000 f838e000 ffff81ff ffff01ff fffe01ff fffe03ff fffe03ff ffff80ff ffffc0ff ffffc0ff
  //   ffff80ff ffff80ff ffff00ff fffe00ff fff800ff fffc00ff fffe00ff 00000000 00400000 001c0000 00010000
  //   000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
  //   contents of rom_18 (hex, n*v repeats v):
  //   00000000 00000000 00000000 00001000 00000400 c0000000 e0000000 e0000000 f0000000 f8000000 fe0fe000
  //   fe1ee000 ff7fc000 ffffc000 ffff81ff ffff01ff fffe03ff fffc03ff fffe03ff ffff81ff ffffc1ff ffffc0ff
  //   ffff80ff ffff80ff ffff01ff fffe01ff fff801ff fffe00ff fffe00ff 00000000 00800000 00180000 00000000
  //   000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
  //   contents of rom_19 (hex, n*v repeats v):
  //   00000000 00000080 00000000 00000000 00000600 80000000 c0000000 c0000000 e0000000 f0000000 ffff0000
  //   fffe0000 ffff8000 ffff0000 ffff81ff ffff01ff fffe03ff fffc33ff fffe07ff ffff83ff ffffc1ff ffffc1ff
  //   ffff81ff ffff83ff ffff03ff fffe03ff fffc03ff fffe01ff ffff01ff 00000000 00800000 00180000 00000000
  //   000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
  //   contents of rom_20 (hex, n*v repeats v):
  //   00000000 0003e8c0 00000020 00000010 00000400 80000380 c0000000 c0000000 e0000000 f0000000 ffff8000
  //   ffff0000 fffc0000 fff80000 ffff81ff ffff03ff fffe03ff fff837ff fffc07ff ffff83ff ffffc3ff ffffc3ff
  //   ffff83ff ffff83ff ffff03ff fffe03ff fffc03ff fffe03ff ffff01ff 00000000 00000000 00000000 00020000
  //   000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
  //   contents of rom_21 (hex, n*v repeats v):
  //   00000000 0183ffc3 000c12f0 000c0018 00000004 80000380 c00001c0 c0000180 c0000300 e0000100 ffff8000
  //   ffff0000 fffe0000 fffc0000 ffff83ff ffff03ff fffe03ff fff03fff fffc27ff ffff83ff ffffc3ff ffffc3ff
  //   ffff83ff ffff03ff ffff03ff fffe03ff fffc03ff fffe03ff ffff03ff 00000000 00000000 00004000 00030000
  //   000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
  //   contents of rom_22 (hex, n*v repeats v):
  //   00000000 01f1c9e7 0038fff3 000f00f9 00070006 80000302 c00001c0 c00001e0 c00001e0 e00001c0 ffffc000
  //   ffff0000 fffe0003 fffc0007 ffff83ff ffff03ff fffc13ff ff807fff fff83fff ffff87ff ffffc7ff ffffc3ff
  //   ffff83ff ffff07ff ffff07ff fffe07ff fffc07ff fffe07ff ffff07ff 00000000 001c0000 000fc000 00018000
  //   000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
  //   contents of rom_23 (hex, n*v repeats v):
  //   00000000 01f8e1ef 007c76ff 000f3fff 0007c01f 80038003 c0000381 c00003c1 c00001f0 e00000f8 ffffc000
  //   ffff8000 fffe000f fffc001f ffff03ff fffe03ff fff01fff ff807fff ffc03fff ffff87ff ffff87ff ffff87ff
  //   ffff87ff ffff07ff fffe07ff fffe07ff fffc07ff ffff07ff ffff07ff 00400000 00fc0000 0007e000 0000e000
  //   000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
  //   contents of rom_24 (hex, n*v repeats v):
  //   00000000 03f8ffff 007c39ff 001f3f7f 0007dfff c003e01f c0010003 c0000380 c00191c0 e00088f8 ffffe000
  //   ffff8001 ffff007f fffe0fff fffe03ff fff803ff ffc03fff ffe0ffff ffc07fff ffff07ff ffff87ff ffff87ff
  //   ffff07ff fffe07ff fffe07ff fffe07ff fffc07ff ffff07ff ffff07ff 07000000 007e0000 0003f000 0000f000
  //   000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
  //   contents of rom_25 (hex, n*v repeats v):
  //   00000000 03fbffff 00fe7ffe 003f1f98 c007cfc0 c001f798 c001f00c c001b104 e0011182 f000d9c1 ffffe000
  //   ffffc01f ffffffff ffffffff fff807ff fff007ff fff03fff fff9ffff fff8ffff fffe0fff ffff07ff ffff07ff
  //   ffff07ff fffc07ff fffc07ff fffc07ff fffc07ff fffe07ff ffff07ff 03000000 003f0000 0001f000 00007e00
  //   000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
  //   contents of rom_26 (hex, n*v repeats v):
  //   00000000 03fffc00 00feff00 003f1f80 e00fc7e0 e001f7f8 e001f00c e001f00c e001f10f f000d9c7 ffffff80
  //   ffffffff ffffffff ffffffff ffff07ff fffc0fff fffe7fff ffffffff ffffffff fffc0fff ffff0fff fffe0fff
  //   fffc0fff fff00fff fff00fff fff00fff fff80fff fffe0fff fffe0fff 01800000 001f0000 0000f800 00007e00
  //   000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
  //   contents of rom_27 (hex, n*v repeats v):
  //   00000000 01fffc00 00ffff80 c03f3fc0 e00fcff0 f003e3f8 e001fbfc e001f3ee f001f80f f800f807 ffffffff
  //   ffffffff ffffffff ffffffff ffffffff ffffffff ffffffff ffffffff ffffffff ffffffff fffe0fff fffc0fff
  //   fff80fff ffff1fff fffe1fff fffc1fff fffc1fff fffe0fff ffffdfff 00f00000 000f8000 00007800 00003e00
  //   000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
  //   contents of rom_28 (hex, n*v repeats v):
  //   00000000 0007fe00 00ffff80 807fffe0 e00fdff8 f003f7fc f000f1fe f001f9fe f001f9ff f800fdff ffffffff
  //   ffffffff ffffffff ffffffff ffffffff ffffffff ffffffff ffffffff ffffffff ffffffff ffffffff ffffffff
  //   ffffffff ffffffff ffffffff ffffffff ffffffff ffffffff ffffffff 00f00000 00000000 00000000 00003f00
  //   000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
  //   contents of rom_29 (hex, n*v repeats v):
  //   00000000 007fff00 801fffc0 c03fffe0 e01ffff8 f807fffc f801f7fe f000fbfe f800fbff f800fdff ffffffff
  //   ffffffff ffffffff ffffffff ffffffff ffffffff ffffffff ffffffff ffffffff ffffffff ffffffff ffffffff
  //   ffffffff ffffffff ffffffff ffffffff ffffffff ffffffff ffffffff 00000000 00000000 00000000 00000e00
  //   000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
  //   contents of rom_30 (hex, n*v repeats v):
  //   00000000 bfffff00 e9ffffc0 f0fffff0 f83ffff8 f807fffe f801ffff f801ffff f800ffff fc007fff ffffffff
  //   ffffffff ffffffff ffffffff ffffffff ffffffff ffffffff ffffffff ffffffff ffffffff ffffffff ffffffff
  //   ffffffff ffffffff ffffffff ffffffff ffffffff ffffffff ffffffff 00000000 00000000 00000000 00000000
  //   000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
  //   contents of rom_31 (hex, n*v repeats v):
  //   00000000 ffffff80 ffffffe0 fffffff0 fffffffc fc0ffffe fc03ffff fc01ffff fc00ffff fe007fff ffffffff
  //   ffffffff ffffffff ffffffff ffffffff ffffffff ffffffff ffffffff ffffffff ffffffff ffffffff ffffffff
  //   ffffffff ffffffff ffffffff ffffffff ffffffff ffffffff ffffffff 00000000 00000000 00000000 00000000
  //   000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
  //   contents of rom_32 (hex, n*v repeats v):
  //   00000000 ffffff80 ffffffe0 fffffff0 fffffffc ff9ffffe fe87ffff fe83ffff ff01ffff ff00ffff ffffffff
  //   ffffffff ffffffff ffffffff ffffffff ffffffff ffffffff ffffffff ffffffff ffffffff ffffffff ffffffff
  //   ffffffff ffffffff ffffffff ffffffff ffffffff ffffffff ffffffff 00000000 00000000 00000000 00000000
  //   000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
endmodule
